// Logisim project Cache.circ as structural Verilog: 12 circuits, main circuit Cache
module LRU (
  input  [15:0] Cnt_0,
  input  [15:0] Cnt_1,
  input  [15:0] Cnt_2,
  input  [15:0] Cnt_3,
  input  Hit_0,
  input  Hit_1,
  input  Hit_2,
  input  Hit_3,
  input  MemRead,
  input  MemWrite,
  input  EN,
  output WE_0,
  output WE_1,
  output WE_2,
  output WE_3
);

  wire [1:0] maxsel_1_max;

  MaxSel maxsel_1 (.Cnt_0(Cnt_0), .Cnt_1(Cnt_1), .Cnt_2(Cnt_2), .Cnt_3(Cnt_3), .Max(maxsel_1_max));
  Renew renew_1 (
    .Hit_0(Hit_0), .Hit_1(Hit_1), .Max(maxsel_1_max), .Hit_2(Hit_2), .Hit_3(Hit_3), .MemRead(MemRead),
    .MemWrite(MemWrite), .EN(EN), .out_9(WE_0), .out_10(WE_1), .out_11(WE_2), .out_12(WE_3));
endmodule

module MaxSel (
  input  [15:0] Cnt_0,
  input  [15:0] Cnt_1,
  input  [15:0] Cnt_2,
  input  [15:0] Cnt_3,
  output [1:0] Max
);

  wire cmp_1_out_3, cmp_2_out_3;
  wire [15:0] cmp_1_out_4, cmp_2_out_4;

  Cmp cmp_1 (.A(Cnt_0), .B(Cnt_1), .out_3(cmp_1_out_3), .out_4(cmp_1_out_4));
  Cmp cmp_2 (.A(Cnt_2), .B(Cnt_3), .out_3(cmp_2_out_3), .out_4(cmp_2_out_4));
  Cmp cmp_3 (.A(cmp_1_out_4), .B(cmp_2_out_4), .out_3(Max[1]));  // open: out_4
  Multiplexer #(.enable("false")) multiplexer_1 (.in0(cmp_1_out_3), .in1(cmp_2_out_3), .out(Max[0]), .sel(Max[1]));
endmodule

module Cmp (
  input  [15:0] A,
  input  [15:0] B,
  output out_3,
  output [15:0] out_4
);

  wire comparator_1_eq, comparator_1_gt, or_1_out;

  Comparator #(.width(16), .mode("unsigned")) comparator_1 (
    .a(A), .b(B), .gt(comparator_1_gt), .eq(comparator_1_eq));  // open: lt
  not not_1 (out_3, or_1_out);
  or or_1 (or_1_out, comparator_1_gt, comparator_1_eq);
  Multiplexer #(.width(16), .enable("false")) multiplexer_1 (.in0(A), .in1(B), .out(out_4), .sel(out_3));
endmodule

module Renew (
  input  Hit_0,
  input  Hit_1,
  input  [1:0] Max,
  input  Hit_2,
  input  Hit_3,
  input  MemRead,
  input  MemWrite,
  input  EN,
  output out_9,
  output out_10,
  output out_11,
  output out_12
);

  wire and_1_out, and_2_out, and_3_out, decoder_1_out0, decoder_1_out1, decoder_1_out2, decoder_1_out3,
       not_1_out, or_1_out, or_2_out;
  wire [1:0] multiplexer_1_out, n4_2_encoder_1_out_5;

  or or_1 (or_1_out, Hit_0, Hit_1, Hit_2, Hit_3);
  and and_1 (and_1_out, or_1_out, MemWrite);
  and and_2 (and_2_out, ~or_1_out, ~MemWrite);  // AND_Gate
  _4_2_Encoder u_4_2_encoder_1 (.a(Hit_3), .b(Hit_2), .c(Hit_1), .d(Hit_0), .out_5(n4_2_encoder_1_out_5));
  Multiplexer #(.width(2), .enable("false")) multiplexer_1 (
    .in0(n4_2_encoder_1_out_5), .in1(Max), .out(multiplexer_1_out), .sel(not_1_out));
  not not_1 (not_1_out, and_1_out);
  or or_2 (or_2_out, and_1_out, and_2_out);
  Decoder #(.select(2), .enable("false")) decoder_1 (
    .out0(decoder_1_out0), .out1(decoder_1_out1), .out2(decoder_1_out2), .out3(decoder_1_out3),
    .sel(multiplexer_1_out));
  and and_3 (and_3_out, or_2_out, EN);
  and and_4 (out_9, decoder_1_out0, and_3_out);
  and and_5 (out_10, decoder_1_out1, and_3_out);
  and and_6 (out_11, decoder_1_out2, and_3_out);
  and and_7 (out_12, decoder_1_out3, and_3_out);
endmodule

module _4_2_Encoder (
  input  a,
  input  b,
  input  c,
  input  d,
  output [1:0] out_5
);

  or or_1 (out_5[1], b, a);
  or or_2 (out_5[0], c, a);
endmodule

module Cache (
  input  [31:0] MemAdd,
  input  [31:0] Indata,
  input  Str,
  input  Clk,
  input  Ld,
  input  Clr,
  output [15:0] All,
  output [15:0] Hit,
  output [31:0] OutData,
  output Stop
);

  wire and_1_out, and_2_out, and_3_out, and_4_out, and_5_out, and_6_out, decoder_1_out0, decoder_1_out1,
       decoder_1_out2, decoder_1_out3, group_1_hit, group_2_hit, group_3_hit, group_4_hit, Hit_t, or_1_out,
       or_2_out, or_3_out, or_4_out;
  wire [31:0] group_1_out_12, group_1_out_13, group_1_out_14, group_1_out_15, group_2_out_12, group_2_out_13,
       group_2_out_14, group_2_out_15, group_3_out_12, group_3_out_13, group_3_out_14, group_3_out_15,
       group_4_out_12, group_4_out_13, group_4_out_14, group_4_out_15, muxforgroup_1_outdata,
       muxforgroup_1_outdata_2, muxforgroup_1_outdata_3, muxforgroup_1_outdata_4, RAM_0, RAM_1, RAM_2, RAM_3;

  RAM u_ram_1 (
    .MuxBlock(MemAdd[3:2]), .MemWrite(Str), .MemRead(Ld), .Hit(Hit_t), .Tag(MemAdd[11:6]),
    .MuxGroup(MemAdd[5:4]), .MemData(Indata), .Clk(Clk), .Reset(Clr), ._4(RAM_3), ._3(RAM_2), ._2(RAM_1),
    .out_13(Stop), ._1(RAM_0));
  and and_1 (and_1_out, Ld, ~Stop);  // AND_Gate
  and and_2 (and_2_out, Hit_t, Ld, ~Stop);  // AND_Gate
  Counter_part #(.width(16), .max('hffff)) counter_1 (
    .count(and_1_out), .Q(All), .clk(Clk), .clr(Clr));  // open: load, D, carry
  Counter_part #(.width(16), .max('hffff)) counter_2 (
    .count(and_2_out), .Q(Hit), .clk(Clk), .clr(Clr));  // open: load, D, carry
  Decoder #(.select(2), .enable("false")) decoder_1 (
    .out0(decoder_1_out0), .out1(decoder_1_out1), .out2(decoder_1_out2), .out3(decoder_1_out3),
    .sel(MemAdd[5:4]));
  or or_1 (or_1_out, Ld, Str);
  or or_2 (or_2_out, Ld, Str);
  or or_3 (or_3_out, Ld, Str);
  or or_4 (or_4_out, Ld, Str);
  and and_3 (and_3_out, or_1_out, decoder_1_out0);
  and and_4 (and_4_out, or_2_out, decoder_1_out1);
  and and_5 (and_5_out, or_3_out, decoder_1_out2);
  and and_6 (and_6_out, or_4_out, decoder_1_out3);
  Group group_1 (
    .in_1(RAM_0), .in_7(RAM_1), .in_8(RAM_2), .in_9(RAM_3), .MemRead(Ld), .MemWrite(Str),
    .out_12(group_1_out_12), .out_13(group_1_out_13), .out_14(group_1_out_14), .out_15(group_1_out_15),
    .Hit(group_1_hit), .Tag(MemAdd[11:6]), .Clk(Clk), .EN(and_3_out), .Stop(Stop), .Reset(Clr));
  Group group_2 (
    .in_1(RAM_0), .in_7(RAM_1), .in_8(RAM_2), .in_9(RAM_3), .MemRead(Ld), .MemWrite(Str),
    .out_12(group_2_out_12), .out_13(group_2_out_13), .out_14(group_2_out_14), .out_15(group_2_out_15),
    .Hit(group_2_hit), .Tag(MemAdd[11:6]), .Clk(Clk), .EN(and_4_out), .Stop(Stop), .Reset(Clr));
  Group group_3 (
    .in_1(RAM_0), .in_7(RAM_1), .in_8(RAM_2), .in_9(RAM_3), .MemRead(Ld), .MemWrite(Str),
    .out_12(group_3_out_12), .out_13(group_3_out_13), .out_14(group_3_out_14), .out_15(group_3_out_15),
    .Hit(group_3_hit), .Tag(MemAdd[11:6]), .Clk(Clk), .EN(and_5_out), .Stop(Stop), .Reset(Clr));
  Group group_4 (
    .in_1(RAM_0), .in_7(RAM_1), .in_8(RAM_2), .in_9(RAM_3), .MemRead(Ld), .MemWrite(Str),
    .out_12(group_4_out_12), .out_13(group_4_out_13), .out_14(group_4_out_14), .out_15(group_4_out_15),
    .Hit(group_4_hit), .Tag(MemAdd[11:6]), .Clk(Clk), .EN(and_6_out), .Stop(Stop), .Reset(Clr));
  MuxForGroup muxforgroup_1 (
    .MemRead(Ld), .Stop(Stop), .Hit_0(group_1_hit), .Hit_1(group_2_hit), .Hit_2(group_3_hit),
    .Hit_3(group_4_hit), .Data_0(group_1_out_12), .Data_0_2(group_2_out_12), .Data_0_3(group_3_out_12),
    .Data_0_4(group_4_out_12), .Data_0_5(group_1_out_13), .Data_0_6(group_2_out_13),
    .Data_0_7(group_3_out_13), .Data_0_8(group_4_out_13), .Data_0_9(group_1_out_14),
    .Data_0_10(group_2_out_14), .Data_0_11(group_3_out_14), .Data_0_12(group_4_out_14),
    .Data_0_13(group_1_out_15), .Data_0_14(group_2_out_15), .Data_0_15(group_3_out_15),
    .Data_0_16(group_4_out_15), .Data_0_17(RAM_0), .Data_0_18(RAM_1), .Data_0_19(RAM_2), .Data_0_20(RAM_3),
    .OutData(muxforgroup_1_outdata), .OutData_2(muxforgroup_1_outdata_2),
    .OutData_3(muxforgroup_1_outdata_3), .OutData_4(muxforgroup_1_outdata_4), .MuxGroup(MemAdd[5:4]),
    .Hit(Hit_t));
  Multiplexer #(.select(2), .width(32), .enable("false")) multiplexer_1 (
    .in0(muxforgroup_1_outdata), .in1(muxforgroup_1_outdata_2), .in2(muxforgroup_1_outdata_3),
    .in3(muxforgroup_1_outdata_4), .out(OutData), .sel(MemAdd[3:2]));

  // Other names for the same wires on the sheet: All_Cnt[15:0] = All; Hit_Cnt[15:0] = Hit;
  //   MuxBlock[1:0] = MemAdd[3:2]; MuxGroup[1:0] = MemAdd[5:4]; Tag[5:0] = MemAdd[11:6]
endmodule

module Counter (
  input  Reset,
  input  Clk,
  input  MemRead,
  input  Hit,
  input  Renew,
  input  EN,
  output [15:0] Data
);

  wire and_1_out, and_2_out, and_3_out, and_4_out, or_1_out;

  and and_1 (and_1_out, EN, MemRead);
  or or_1 (or_1_out, and_2_out, and_3_out);
  and and_2 (and_2_out, MemRead, EN, Renew);
  and and_3 (and_3_out, MemRead, EN, Hit);
  Counter_part #(.width(16), .max('hffff)) counter_1 (
    .load(or_1_out), .D({16{1'b0}}), .count(and_4_out), .Q(Data), .clk(Clk), .clr(Reset));  // open: carry
  and and_4 (and_4_out, and_1_out, ~or_1_out);  // AND_Gate
endmodule

module Block (
  input  [5:0] InTag,
  input  [31:0] InData_0,
  input  [31:0] InData_1,
  input  [31:0] InData_2,
  input  [31:0] InData_3,
  input  Reset,
  input  Clk,
  input  EN,
  output v,
  output [5:0] OutTag,
  output [31:0] OutData_0,
  output [31:0] OutData_1,
  output [31:0] OutData_2,
  output [31:0] OutData_3
);

  Register #(.width(32)) register_1 (.D(InData_0), .en(EN), .Q(OutData_0), .clk(Clk), .clr(Reset));
  Register #(.width(1)) register_2 (.D(1'b1), .en(EN), .Q(v), .clk(Clk), .clr(Reset));
  Register #(.width(6)) register_3 (.D(InTag), .en(EN), .Q(OutTag), .clk(Clk), .clr(Reset));
  Register #(.width(32)) register_4 (.D(InData_1), .en(EN), .Q(OutData_1), .clk(Clk), .clr(Reset));
  Register #(.width(32)) register_5 (.D(InData_2), .en(EN), .Q(OutData_2), .clk(Clk), .clr(Reset));
  Register #(.width(32)) register_6 (.D(InData_3), .en(EN), .Q(OutData_3), .clk(Clk), .clr(Reset));
endmodule

module Group (
  input  [31:0] in_1,
  input  [5:0] Tag,
  input  Clk,
  input  EN,
  input  Stop,
  input  Reset,
  input  [31:0] in_7,
  input  [31:0] in_8,
  input  [31:0] in_9,
  input  MemRead,
  input  MemWrite,
  output [31:0] out_12,
  output [31:0] out_13,
  output [31:0] out_14,
  output [31:0] out_15,
  output Hit
);

  wire and_1_out, and_2_out, and_3_out, and_4_out, and_5_out, and_6_out, and_7_out, and_8_out, and_13_out,
       block_1_v, block_2_v, block_3_v, block_4_v, comparator_1_eq, comparator_2_eq, comparator_3_eq,
       comparator_4_eq, Hit_0, Hit_1, Hit_2, Hit_3, muxforblock_1_out_21, WE_0, WE_1, WE_2, WE_3;
  wire [5:0] block_1_outtag, block_2_outtag, block_3_outtag, block_4_outtag;
  wire [15:0] Cnt_0, Cnt_1, Cnt_2, Cnt_3;
  wire [31:0] block_1_outdata_0, block_1_outdata_1, block_1_outdata_2, block_1_outdata_3, block_2_outdata_0,
       block_2_outdata_1, block_2_outdata_2, block_2_outdata_3, block_3_outdata_0, block_3_outdata_1,
       block_3_outdata_2, block_3_outdata_3, block_4_outdata_0, block_4_outdata_1, block_4_outdata_2,
       block_4_outdata_3;

  and and_1 (and_1_out, ~Stop, EN);  // AND_Gate
  and and_2 (and_2_out, ~Stop, EN);  // AND_Gate
  and and_3 (and_3_out, ~Stop, EN);  // AND_Gate
  and and_4 (and_4_out, ~Stop, EN);  // AND_Gate
  Counter counter_1 (
    .Reset(Reset), .Clk(Clk), .MemRead(MemRead), .Hit(Hit_0), .Renew(WE_0), .Data(Cnt_0), .EN(and_1_out));
  Counter counter_2 (
    .Reset(Reset), .Clk(Clk), .MemRead(MemRead), .Hit(Hit_1), .Renew(WE_1), .Data(Cnt_1), .EN(and_2_out));
  Counter counter_3 (
    .Reset(Reset), .Clk(Clk), .MemRead(MemRead), .Hit(Hit_2), .Renew(WE_2), .Data(Cnt_2), .EN(and_3_out));
  Counter counter_4 (
    .Reset(Reset), .Clk(Clk), .MemRead(MemRead), .Hit(Hit_3), .Renew(WE_3), .Data(Cnt_3), .EN(and_4_out));
  and and_5 (and_5_out, EN, ~Stop, WE_0);  // AND_Gate
  and and_6 (and_6_out, EN, ~Stop, WE_1);  // AND_Gate
  and and_7 (and_7_out, EN, ~Stop, WE_2);  // AND_Gate
  and and_8 (and_8_out, EN, ~Stop, WE_3);  // AND_Gate
  Block block_1 (
    .Reset(Reset), .Clk(Clk), .EN(and_5_out), .InTag(Tag), .InData_0(in_1), .InData_1(in_7), .InData_2(in_8),
    .InData_3(in_9), .v(block_1_v), .OutTag(block_1_outtag), .OutData_0(block_1_outdata_0),
    .OutData_1(block_1_outdata_1), .OutData_2(block_1_outdata_2), .OutData_3(block_1_outdata_3));
  Block block_2 (
    .Reset(Reset), .Clk(Clk), .EN(and_6_out), .InTag(Tag), .InData_0(in_1), .InData_1(in_7), .InData_2(in_8),
    .InData_3(in_9), .v(block_2_v), .OutTag(block_2_outtag), .OutData_0(block_2_outdata_0),
    .OutData_1(block_2_outdata_1), .OutData_2(block_2_outdata_2), .OutData_3(block_2_outdata_3));
  Block block_3 (
    .Reset(Reset), .Clk(Clk), .EN(and_7_out), .InTag(Tag), .InData_0(in_1), .InData_1(in_7), .InData_2(in_8),
    .InData_3(in_9), .v(block_3_v), .OutTag(block_3_outtag), .OutData_0(block_3_outdata_0),
    .OutData_1(block_3_outdata_1), .OutData_2(block_3_outdata_2), .OutData_3(block_3_outdata_3));
  Block block_4 (
    .Reset(Reset), .Clk(Clk), .EN(and_8_out), .InTag(Tag), .InData_0(in_1), .InData_1(in_7), .InData_2(in_8),
    .InData_3(in_9), .v(block_4_v), .OutTag(block_4_outtag), .OutData_0(block_4_outdata_0),
    .OutData_1(block_4_outdata_1), .OutData_2(block_4_outdata_2), .OutData_3(block_4_outdata_3));
  Comparator #(.width(6)) comparator_1 (.a(block_1_outtag), .b(Tag), .eq(comparator_1_eq));  // open: gt, lt
  Comparator #(.width(6)) comparator_2 (.a(block_2_outtag), .b(Tag), .eq(comparator_2_eq));  // open: gt, lt
  Comparator #(.width(6)) comparator_3 (.a(block_3_outtag), .b(Tag), .eq(comparator_3_eq));  // open: gt, lt
  Comparator #(.width(6)) comparator_4 (.a(block_4_outtag), .b(Tag), .eq(comparator_4_eq));  // open: gt, lt
  and and_9 (Hit_0, comparator_1_eq, block_1_v);
  and and_10 (Hit_1, comparator_2_eq, block_2_v);
  and and_11 (Hit_2, comparator_3_eq, block_3_v);
  and and_12 (Hit_3, comparator_4_eq, block_4_v);
  and and_13 (and_13_out, ~Stop, EN);  // AND_Gate
  MuxForBlock muxforblock_1 (
    .Hit_0(Hit_0), .Hit_1(Hit_1), .Hit_2(Hit_2), .Hit_3(Hit_3), .Data_0(block_1_outdata_0),
    .Data_0_2(block_2_outdata_0), .Data_0_3(block_3_outdata_0), .Data_0_4(block_4_outdata_0),
    .OutData(out_12), .Data_0_5(block_1_outdata_1), .Data_0_6(block_2_outdata_1), .OutData_2(out_13),
    .Data_0_7(block_3_outdata_1), .Data_0_8(block_4_outdata_1), .Data_0_9(block_1_outdata_2),
    .Data_0_10(block_2_outdata_2), .OutData_3(out_14), .Data_0_11(block_3_outdata_2),
    .Data_0_12(block_4_outdata_2), .Data_0_13(block_1_outdata_3), .Data_0_14(block_2_outdata_3),
    .OutData_4(out_15), .Data_0_15(block_3_outdata_3), .Data_0_16(block_4_outdata_3),
    .out_21(muxforblock_1_out_21));
  LRU lru_1 (
    .Cnt_0(Cnt_0), .Cnt_1(Cnt_1), .Cnt_2(Cnt_2), .Cnt_3(Cnt_3), .Hit_0(Hit_0), .Hit_1(Hit_1), .Hit_2(Hit_2),
    .Hit_3(Hit_3), .MemRead(MemRead), .MemWrite(MemWrite), .EN(and_13_out), .WE_0(WE_0), .WE_1(WE_1),
    .WE_2(WE_2), .WE_3(WE_3));
  and and_14 (Hit, muxforblock_1_out_21, EN);

  // Other names for the same wires on the sheet: InData_0[31:0] = in_1; InData_1[31:0] = in_7; InData_2[31:0] = in_8;
  //   InData_3[31:0] = in_9
endmodule

module MuxForBlock (
  input  Hit_0,
  input  Hit_1,
  input  Hit_2,
  input  Hit_3,
  input  [31:0] Data_0,
  input  [31:0] Data_0_2,
  input  [31:0] Data_0_3,
  input  [31:0] Data_0_4,
  input  [31:0] Data_0_5,
  input  [31:0] Data_0_6,
  input  [31:0] Data_0_7,
  input  [31:0] Data_0_8,
  input  [31:0] Data_0_9,
  input  [31:0] Data_0_10,
  input  [31:0] Data_0_11,
  input  [31:0] Data_0_12,
  input  [31:0] Data_0_13,
  input  [31:0] Data_0_14,
  input  [31:0] Data_0_15,
  input  [31:0] Data_0_16,
  output out_21,
  output [31:0] OutData,
  output [31:0] OutData_2,
  output [31:0] OutData_3,
  output [31:0] OutData_4
);

  wire [1:0] n4_2_encoder_1_out_5;
  wire [31:0] multiplexer_1_out, multiplexer_2_out, multiplexer_3_out, multiplexer_4_out;

  or or_1 (out_21, Hit_0, Hit_1, Hit_2, Hit_3);
  _4_2_Encoder u_4_2_encoder_1 (.a(Hit_3), .b(Hit_2), .c(Hit_1), .d(Hit_0), .out_5(n4_2_encoder_1_out_5));
  Multiplexer #(.select(2), .width(32), .enable("false")) multiplexer_1 (
    .in0(Data_0), .in1(Data_0_2), .in2(Data_0_3), .in3(Data_0_4), .out(multiplexer_1_out),
    .sel(n4_2_encoder_1_out_5));
  Multiplexer #(.select(2), .width(32), .enable("false")) multiplexer_2 (
    .in0(Data_0_5), .in1(Data_0_6), .in2(Data_0_7), .in3(Data_0_8), .out(multiplexer_2_out),
    .sel(n4_2_encoder_1_out_5));
  Multiplexer #(.select(2), .width(32), .enable("false")) multiplexer_3 (
    .in0(Data_0_9), .in1(Data_0_10), .in2(Data_0_11), .in3(Data_0_12), .out(multiplexer_3_out),
    .sel(n4_2_encoder_1_out_5));
  Multiplexer #(.select(2), .width(32), .enable("false")) multiplexer_4 (
    .in0(Data_0_13), .in1(Data_0_14), .in2(Data_0_15), .in3(Data_0_16), .out(multiplexer_4_out),
    .sel(n4_2_encoder_1_out_5));
  Multiplexer #(.width(32), .enable("false")) multiplexer_5 (
    .in0({32{1'b0}}), .in1(multiplexer_1_out), .out(OutData), .sel(out_21));
  Multiplexer #(.width(32), .enable("false")) multiplexer_6 (
    .in0({32{1'b0}}), .in1(multiplexer_2_out), .out(OutData_2), .sel(out_21));
  Multiplexer #(.width(32), .enable("false")) multiplexer_7 (
    .in0({32{1'b0}}), .in1(multiplexer_3_out), .out(OutData_3), .sel(out_21));
  Multiplexer #(.width(32), .enable("false")) multiplexer_8 (
    .in0({32{1'b0}}), .in1(multiplexer_4_out), .out(OutData_4), .sel(out_21));
endmodule

module RAM (
  input  [1:0] MuxBlock,
  input  MemWrite,
  input  MemRead,
  input  Hit,
  input  [5:0] Tag,
  input  [1:0] MuxGroup,
  input  [31:0] MemData,
  input  Clk,
  input  Reset,
  output [31:0] _4,
  output [31:0] _3,
  output [31:0] _2,
  output out_13,
  output [31:0] _1
);

  wire _1_t, _2_t, _3_t, _4_t, and_1_out, and_2_out, counter_1_carry, not_1_out, not_2_out;
  wire [9:0] adder_1_out, adder_2_out, adder_3_out, adder_4_out, multiplexer_1_out;
  wire [31:0] ram_1_data, ram_2_data, ram_3_data, ram_4_data;

  and and_1 (and_1_out, MemRead, not_1_out);
  not not_1 (not_1_out, Hit);
  Counter_part #(.width(3), .max('h5)) counter_1 (
    .count(and_1_out), .carry(counter_1_carry), .clk(Clk), .clr(Reset));  // open: load, D, Q
  and and_2 (and_2_out, MemRead, Hit);
  and and_3 (out_13, and_1_out, not_2_out);
  not not_2 (not_2_out, counter_1_carry);
  Demultiplexer #(.select(2)) demultiplexer_1 (
    .out0(_1_t), .out1(_2_t), .out2(_3_t), .out3(_4_t), .in(MemWrite), .sel(MuxBlock));  // open: en
  Multiplexer #(.width(10), .enable("false")) multiplexer_1 (
    .in0({Tag, MuxGroup, 2'b00}), .in1({10{1'b0}}), .out(multiplexer_1_out), .sel(and_2_out));
  Adder #(.width(10)) adder_1 (.a(10'h3), .b(multiplexer_1_out), .out(adder_1_out));  // open: cin, cout
  Adder #(.width(10)) adder_2 (.a(10'h2), .b(multiplexer_1_out), .out(adder_2_out));  // open: cin, cout
  Adder #(.width(10)) adder_3 (.a(10'h1), .b(multiplexer_1_out), .out(adder_3_out));  // open: cin, cout
  Adder #(.width(10)) adder_4 (.a({10{1'b0}}), .b(multiplexer_1_out), .out(adder_4_out));  // open: cin, cout
  RAM_part #(.addrWidth(10), .dataWidth(32), .bus("separate")) ram_1 (
    .addr(adder_1_out), .din(MemData), .data(ram_1_data), .str(_4_t), .clk(Clk), .clr(Reset));  // open: sel, ld
  RAM_part #(.addrWidth(10), .dataWidth(32), .bus("separate")) ram_2 (
    .addr(adder_2_out), .din(MemData), .data(ram_2_data), .str(_3_t), .clk(Clk), .clr(Reset));  // open: sel, ld
  RAM_part #(.addrWidth(10), .dataWidth(32), .bus("separate")) ram_3 (
    .addr(adder_3_out), .din(MemData), .data(ram_3_data), .str(_2_t), .clk(Clk), .clr(Reset));  // open: sel, ld
  RAM_part #(.addrWidth(10), .dataWidth(32), .bus("separate")) ram_4 (
    .addr(adder_4_out), .din(MemData), .data(ram_4_data), .str(_1_t), .clk(Clk), .clr(Reset));  // open: sel, ld
  Multiplexer #(.width(32), .enable("false")) multiplexer_2 (.in0(ram_1_data), .in1(MemData), .out(_4), .sel(_4_t));
  Multiplexer #(.width(32), .enable("false")) multiplexer_3 (.in0(ram_2_data), .in1(MemData), .out(_3), .sel(_3_t));
  Multiplexer #(.width(32), .enable("false")) multiplexer_4 (.in0(ram_3_data), .in1(MemData), .out(_2), .sel(_2_t));
  Multiplexer #(.width(32), .enable("false")) multiplexer_5 (.in0(ram_4_data), .in1(MemData), .out(_1), .sel(_1_t));

  // Other names for the same wires on the sheet: Data[31:0] = MemData
endmodule

module MuxForGroup (
  input  [1:0] MuxGroup,
  input  MemRead,
  input  Stop,
  input  Hit_0,
  input  Hit_1,
  input  Hit_2,
  input  Hit_3,
  input  [31:0] Data_0,
  input  [31:0] Data_0_2,
  input  [31:0] Data_0_3,
  input  [31:0] Data_0_4,
  input  [31:0] Data_0_5,
  input  [31:0] Data_0_6,
  input  [31:0] Data_0_7,
  input  [31:0] Data_0_8,
  input  [31:0] Data_0_9,
  input  [31:0] Data_0_10,
  input  [31:0] Data_0_11,
  input  [31:0] Data_0_12,
  input  [31:0] Data_0_13,
  input  [31:0] Data_0_14,
  input  [31:0] Data_0_15,
  input  [31:0] Data_0_16,
  input  [31:0] Data_0_17,
  input  [31:0] Data_0_18,
  input  [31:0] Data_0_19,
  input  [31:0] Data_0_20,
  output Hit,
  output [31:0] OutData,
  output [31:0] OutData_2,
  output [31:0] OutData_3,
  output [31:0] OutData_4
);

  wire and_1_out;
  wire [31:0] multiplexer_2_out, multiplexer_3_out, multiplexer_4_out, multiplexer_5_out, multiplexer_6_out,
       multiplexer_7_out, multiplexer_8_out, multiplexer_9_out;

  Multiplexer #(.select(2), .enable("false")) multiplexer_1 (
    .in0(Hit_0), .in1(Hit_1), .in2(Hit_2), .in3(Hit_3), .out(Hit), .sel(MuxGroup));
  Multiplexer #(.select(2), .width(32), .enable("false")) multiplexer_2 (
    .in0(Data_0), .in1(Data_0_2), .in2(Data_0_3), .in3(Data_0_4), .out(multiplexer_2_out), .sel(MuxGroup));
  Multiplexer #(.select(2), .width(32), .enable("false")) multiplexer_3 (
    .in0(Data_0_5), .in1(Data_0_6), .in2(Data_0_7), .in3(Data_0_8), .out(multiplexer_3_out), .sel(MuxGroup));
  Multiplexer #(.select(2), .width(32), .enable("false")) multiplexer_4 (
    .in0(Data_0_9), .in1(Data_0_10), .in2(Data_0_11), .in3(Data_0_12), .out(multiplexer_4_out), .sel(MuxGroup));
  Multiplexer #(.select(2), .width(32), .enable("false")) multiplexer_5 (
    .in0(Data_0_13), .in1(Data_0_14), .in2(Data_0_15), .in3(Data_0_16), .out(multiplexer_5_out),
    .sel(MuxGroup));
  Multiplexer #(.width(32), .enable("false")) multiplexer_6 (
    .in0(Data_0_17), .in1(multiplexer_2_out), .out(multiplexer_6_out), .sel(Hit));
  Multiplexer #(.width(32), .enable("false")) multiplexer_7 (
    .in0(Data_0_18), .in1(multiplexer_3_out), .out(multiplexer_7_out), .sel(Hit));
  Multiplexer #(.width(32), .enable("false")) multiplexer_8 (
    .in0(Data_0_19), .in1(multiplexer_4_out), .out(multiplexer_8_out), .sel(Hit));
  Multiplexer #(.width(32), .enable("false")) multiplexer_9 (
    .in0(Data_0_20), .in1(multiplexer_5_out), .out(multiplexer_9_out), .sel(Hit));
  and and_1 (and_1_out, MemRead, ~Stop);  // AND_Gate
  Multiplexer #(.width(32), .enable("false")) multiplexer_10 (
    .in0({32{1'b0}}), .in1(multiplexer_6_out), .out(OutData), .sel(and_1_out));
  Multiplexer #(.width(32), .enable("false")) multiplexer_11 (
    .in0({32{1'b0}}), .in1(multiplexer_7_out), .out(OutData_2), .sel(and_1_out));
  Multiplexer #(.width(32), .enable("false")) multiplexer_12 (
    .in0({32{1'b0}}), .in1(multiplexer_8_out), .out(OutData_3), .sel(and_1_out));
  Multiplexer #(.width(32), .enable("false")) multiplexer_13 (
    .in0({32{1'b0}}), .in1(multiplexer_9_out), .out(OutData_4), .sel(and_1_out));

  // Other names for the same wires on the sheet: RAM_0[31:0] = Data_0_17; RAM_1[31:0] = Data_0_18;
  //   RAM_2[31:0] = Data_0_19; RAM_3[31:0] = Data_0_20
endmodule
