// Logisim project CPU.circ as structural Verilog: 12 circuits, main circuit main
module GRF (
  input  [4:0] A1,
  input  clk,
  input  reset,
  input  we,
  input  [4:0] A2,
  input  [4:0] A3,
  input  [31:0] WD,
  output [31:0] RD1,
  output [31:0] RD2
);

  wire [31:0] I0, I1, I2, I3, I4, I5, I6, I7, I8, I9, I10, I11, I12, I13, I14, I15, I16, I17, I18, I19, I20,
       I21, I22, I23, I24, I25, I26, I27, I28, I29, I30, I31, O0, O1, O2, O3, O4, O5, O6, O7, O8, O9, O10,
       O11, O12, O13, O14, O15, O16, O17, O18, O19, O20, O21, O22, O23, O24, O25, O26, O27, O28, O29, O30,
       O31;

  Demultiplexer #(.select(5), .width(32), .tristate("true")) demultiplexer_1 (
    .out0(I0), .out1(I1), .out2(I2), .out3(I3), .out4(I4), .out5(I5), .out6(I6), .out7(I7), .out8(I8),
    .out9(I9), .out10(I10), .out11(I11), .out12(I12), .out13(I13), .out14(I14), .out15(I15), .out16(I16),
    .out17(I17), .out18(I18), .out19(I19), .out20(I20), .out21(I21), .out22(I22), .out23(I23), .out24(I24),
    .out25(I25), .out26(I26), .out27(I27), .out28(I28), .out29(I29), .out30(I30), .out31(I31), .in(WD),
    .sel(A3));  // open: en
  Multiplexer #(.select(5), .width(32)) multiplexer_1 (
    .in0(O0), .in1(O1), .in2(O2), .in3(O3), .in4(O4), .in5(O5), .in6(O6), .in7(O7), .in8(O8), .in9(O9),
    .in10(O10), .in11(O11), .in12(O12), .in13(O13), .in14(O14), .in15(O15), .in16(O16), .in17(O17),
    .in18(O18), .in19(O19), .in20(O20), .in21(O21), .in22(O22), .in23(O23), .in24(O24), .in25(O25),
    .in26(O26), .in27(O27), .in28(O28), .in29(O29), .in30(O30), .in31(O31), .out(RD2), .sel(A2));  // open: en
  Multiplexer #(.select(5), .width(32)) multiplexer_2 (
    .in0(O0), .in1(O1), .in2(O2), .in3(O3), .in4(O4), .in5(O5), .in6(O6), .in7(O7), .in8(O8), .in9(O9),
    .in10(O10), .in11(O11), .in12(O12), .in13(O13), .in14(O14), .in15(O15), .in16(O16), .in17(O17),
    .in18(O18), .in19(O19), .in20(O20), .in21(O21), .in22(O22), .in23(O23), .in24(O24), .in25(O25),
    .in26(O26), .in27(O27), .in28(O28), .in29(O29), .in30(O30), .in31(O31), .out(RD1), .sel(A1));  // open: en
  Register #(.width(32)) register_1 (.D({32{1'b0}}), .en(we), .Q(O0), .clk(clk), .clr(reset));
  Register #(.width(32)) register_2 (.D(I8), .en(we), .Q(O8), .clk(clk), .clr(reset));
  Register #(.width(32)) register_3 (.D(I16), .en(we), .Q(O16), .clk(clk), .clr(reset));
  Register #(.width(32)) register_4 (.D(I24), .en(we), .Q(O24), .clk(clk), .clr(reset));
  Register #(.width(32)) register_5 (.D(I1), .en(we), .Q(O1), .clk(clk), .clr(reset));
  Register #(.width(32)) register_6 (.D(I9), .en(we), .Q(O9), .clk(clk), .clr(reset));
  Register #(.width(32)) register_7 (.D(I17), .en(we), .Q(O17), .clk(clk), .clr(reset));
  Register #(.width(32)) register_8 (.D(I25), .en(we), .Q(O25), .clk(clk), .clr(reset));
  Register #(.width(32)) register_9 (.D(I2), .en(we), .Q(O2), .clk(clk), .clr(reset));
  Register #(.width(32)) register_10 (.D(I10), .en(we), .Q(O10), .clk(clk), .clr(reset));
  Register #(.width(32)) register_11 (.D(I18), .en(we), .Q(O18), .clk(clk), .clr(reset));
  Register #(.width(32)) register_12 (.D(I26), .en(we), .Q(O26), .clk(clk), .clr(reset));
  Register #(.width(32)) register_13 (.D(I3), .en(we), .Q(O3), .clk(clk), .clr(reset));
  Register #(.width(32)) register_14 (.D(I11), .en(we), .Q(O11), .clk(clk), .clr(reset));
  Register #(.width(32)) register_15 (.D(I19), .en(we), .Q(O19), .clk(clk), .clr(reset));
  Register #(.width(32)) register_16 (.D(I27), .en(we), .Q(O27), .clk(clk), .clr(reset));
  Register #(.width(32)) register_17 (.D(I4), .en(we), .Q(O4), .clk(clk), .clr(reset));
  Register #(.width(32)) register_18 (.D(I12), .en(we), .Q(O12), .clk(clk), .clr(reset));
  Register #(.width(32)) register_19 (.D(I20), .en(we), .Q(O20), .clk(clk), .clr(reset));
  Register #(.width(32)) register_20 (.D(I28), .en(we), .Q(O28), .clk(clk), .clr(reset));
  Register #(.width(32)) register_21 (.D(I5), .en(we), .Q(O5), .clk(clk), .clr(reset));
  Register #(.width(32)) register_22 (.D(I13), .en(we), .Q(O13), .clk(clk), .clr(reset));
  Register #(.width(32)) register_23 (.D(I21), .en(we), .Q(O21), .clk(clk), .clr(reset));
  Register #(.width(32)) register_24 (.D(I29), .en(we), .Q(O29), .clk(clk), .clr(reset));
  Register #(.width(32)) register_25 (.D(I6), .en(we), .Q(O6), .clk(clk), .clr(reset));
  Register #(.width(32)) register_26 (.D(I14), .en(we), .Q(O14), .clk(clk), .clr(reset));
  Register #(.width(32)) register_27 (.D(I22), .en(we), .Q(O22), .clk(clk), .clr(reset));
  Register #(.width(32)) register_28 (.D(I30), .en(we), .Q(O30), .clk(clk), .clr(reset));
  Register #(.width(32)) register_29 (.D(I7), .en(we), .Q(O7), .clk(clk), .clr(reset));
  Register #(.width(32)) register_30 (.D(I15), .en(we), .Q(O15), .clk(clk), .clr(reset));
  Register #(.width(32)) register_31 (.D(I23), .en(we), .Q(O23), .clk(clk), .clr(reset));
  Register #(.width(32)) register_32 (.D(I31), .en(we), .Q(O31), .clk(clk), .clr(reset));
endmodule

module main (
  input  Reset,
  output [31:0] Instr,
  output RegWrite,
  output [4:0] RegAddr,
  output [31:0] RegData,
  output MemWrite,
  output [4:0] MemAddr,
  output [31:0] MemData
);

  wire ALUSrc, beq, bgtz, Clk_prime, equal, j_jal, jr, lb, MemRead, sb;
  wire [1:0] EXTOp, RegDst, RegSrc;
  wire [3:0] controller_1_aluop;
  wire [4:0] decoder_1_rd, decoder_1_rs, decoder_1_rt, n32_5_1_output_5;
  wire [5:0] decoder_1_func, decoder_1_op;
  wire [15:0] decoder_1_imm_16;
  wire [25:0] Add_26;
  wire [31:0] ALUOut, EXTOut, MemOut, multiplexer_3_out, npc_1_npc, pc_1_output, pc_4, RD1;

  Clock clock_1 (.out(Clk_prime));
  NPC npc_1 (
    .imm_26(Add_26), .PC(pc_1_output), .RD(RD1), .PC_4(pc_4), .NPC(npc_1_npc), .j_jal(j_jal), .bgtz(bgtz),
    .beq(beq), .jr(jr), .equal(equal));
  PC pc_1 (.Input(npc_1_npc), .Output(pc_1_output), .Reset(Reset), .CLK(Clk_prime));
  _32__5 u_32_5_1 (.Input_32(pc_1_output), .Output_5(n32_5_1_output_5));
  ROM #(.addrWidth(5), .dataWidth(32)) rom_1 (.addr(n32_5_1_output_5), .data(Instr));  // open: sel
  Decoder decoder_1 (
    .inst(Instr), .Op(decoder_1_op), .Func(decoder_1_func), .rs(decoder_1_rs), .rt(decoder_1_rt),
    .rd(decoder_1_rd), .imm_16(decoder_1_imm_16), .add_26(Add_26));  // open: shamt
  Multiplexer #(.select(2), .width(5), .enable("false")) multiplexer_1 (
    .in0(decoder_1_rt), .in1(decoder_1_rd), .in2({5{1'b1}}), .out(RegAddr), .sel(RegDst));  // open: in3
  EXT ext_1 (.Input_16(decoder_1_imm_16), .Output_32(EXTOut), .EXT_Op(EXTOp));
  Controller controller_1 (
    .Op(decoder_1_op), .Func(decoder_1_func), .EXTOp(EXTOp), .ALUOp(controller_1_aluop), .ALUSrc(ALUSrc),
    .RegDst(RegDst), .RegSrc(RegSrc), .RegWrite(RegWrite), .MemRead(MemRead), .MemWrite(MemWrite),
    .b_j_jal(j_jal), .b_beq(beq), .b_jr(jr), .b_bgtz(bgtz), .lb(lb), .sb(sb));
  Multiplexer #(.select(2), .width(32), .enable("false")) multiplexer_2 (
    .in0(MemOut), .in1({ALUOut[31:7], MemAddr, ALUOut[1:0]}), .in2(EXTOut), .in3(pc_4), .out(RegData),
    .sel(RegSrc));
  GRF grf_1 (
    .A1(decoder_1_rs), .A2(decoder_1_rt), .A3(RegAddr), .WD(RegData), .RD1(RD1), .RD2(MemData),
    .clk(Clk_prime), .reset(Reset), .we(RegWrite));
  Multiplexer #(.width(32), .enable("false")) multiplexer_3 (
    .in0(EXTOut), .in1(MemData), .out(multiplexer_3_out), .sel(ALUSrc));
  ALU alu_1 (
    .A(RD1), .B(multiplexer_3_out), .ALUOp(controller_1_aluop), .out_5({ALUOut[31:7], MemAddr, ALUOut[1:0]}),
    .out_4(equal));
  DM dm_1 (
    .in_5({ALUOut[31:7], MemAddr, ALUOut[1:0]}), .in_6(MemData), .RD(MemOut), .lb(lb), .in_2(Clk_prime),
    .reset(Reset), .sb(sb), .MemW(MemWrite), .MemR(MemRead));

  // Other names for the same wires on the sheet: ALUOut[6:2] = MemAddr

  // Notes on the sheet:
  //   contents of rom_1 (hex, n*v repeats v):
  //   34011234 24023000 400008
endmodule

module PC (
  input  [31:0] Input,
  input  Reset,
  input  CLK,
  output [31:0] Output
);

  wire [31:0] multiplexer_1_out;

  Multiplexer #(.width(32), .enable("false")) multiplexer_1 (
    .in0(Input), .in1(32'h3000), .out(multiplexer_1_out), .sel(Reset));
  Register #(.width(32)) register_1 (.D(multiplexer_1_out), .Q(Output), .clk(CLK));  // open: en, clr
endmodule

module NPC (
  input  j_jal,
  input  bgtz,
  input  beq,
  input  jr,
  input  equal,
  input  [25:0] imm_26,
  input  [31:0] PC,
  input  [31:0] RD,
  output [31:0] PC_4,
  output [31:0] NPC
);

  wire and_1_out, and_2_out, comparator_1_gt;
  wire [1:0] NPCOp;
  wire [27:0] bit_extender_2_out, n2_28_1_out_2;
  wire [31:0] adder_2_out, bit_extender_1_out, n2_32_1_out_2;

  and and_1 (and_1_out, beq, equal);
  and and_2 (and_2_out, bgtz, comparator_1_gt);
  Comparator #(.width(32)) comparator_1 (.a(RD), .b({32{1'b0}}), .gt(comparator_1_gt));  // open: eq, lt
  Adder #(.width(32)) adder_1 (.a(PC), .b(32'h4), .out(PC_4));  // open: cin, cout
  or or_1 (NPCOp[1], j_jal, jr);
  assign bit_extender_1_out = {{16{imm_26[15]}}, imm_26[15:0]};  // Bit_Extender bit_extender_1
  _2_32 u_2_32_1 (.in_1(bit_extender_1_out), .out_2(n2_32_1_out_2));
  _2_28 u_2_28_1 (.in_1(bit_extender_2_out), .out_2(n2_28_1_out_2));
  assign bit_extender_2_out = {{2{imm_26[25]}}, imm_26};  // Bit_Extender bit_extender_2
  or or_2 (NPCOp[0], jr, and_1_out, and_2_out);
  Adder #(.width(32)) adder_2 (.a(PC_4), .b(n2_32_1_out_2), .out(adder_2_out));  // open: cin, cout
  Multiplexer #(.select(2), .width(32), .enable("false")) multiplexer_1 (
    .in0(PC_4), .in1(adder_2_out), .in2({PC[31:28], n2_28_1_out_2}), .in3(RD), .out(NPC), .sel(NPCOp));
endmodule

module _2_28 (
  input  [27:0] in_1,
  output [27:0] out_2
);

  Shifter #(.width(28)) shifter_1 (.in(in_1), .\dist (5'b00010), .out(out_2));
endmodule

module _2_32 (
  input  [31:0] in_1,
  output [31:0] out_2
);

  Shifter #(.width(32)) shifter_1 (.in(in_1), .\dist (5'b00010), .out(out_2));
endmodule

module _32__5 (
  input  [31:0] Input_32,
  output [4:0] Output_5
);

  wire [31:0] subtractor_1_out;

  Subtractor #(.width(32)) subtractor_1 (
    .a(Input_32), .b(32'h3000), .out({subtractor_1_out[31:7], Output_5, subtractor_1_out[1:0]}));  // open: bin, bout
endmodule

module Decoder (
  input  [31:0] inst,
  output [5:0] Op,
  output [5:0] Func,
  output [4:0] rs,
  output [4:0] rt,
  output [4:0] rd,
  output [15:0] imm_16,
  output [25:0] add_26,
  output [4:0] shamt
);


  assign add_26 = inst[25:0];
  assign Func = inst[5:0];
  assign imm_16 = inst[15:0];
  assign Op = inst[31:26];
  assign rd = inst[15:11];
  assign rs = inst[25:21];
  assign rt = inst[20:16];
  assign shamt = inst[10:6];
endmodule

module Controller (
  input  [5:0] Op,
  input  [5:0] Func,
  output [3:0] ALUOp,
  output ALUSrc,
  output [1:0] RegDst,
  output [1:0] RegSrc,
  output RegWrite,
  output MemRead,
  output MemWrite,
  output b_j_jal,
  output b_beq,
  output b_jr,
  output b_bgtz,
  output lb,
  output sb,
  output [1:0] EXTOp
);

  wire addiu_out, addu_out, j_out, jal_out, lui_out, lw_out, ori_out, subu_out, sw_out;

  and lw (lw_out, Op[5], ~Op[4], ~Op[3], ~Op[2], Op[1], Op[0]);  // AND_Gate
  and u_lb (lb, Op[5], ~Op[4], ~Op[3], ~Op[2], ~Op[1], ~Op[0]);  // AND_Gate
  and sw (sw_out, Op[5], ~Op[4], Op[3], ~Op[2], Op[1], Op[0]);  // AND_Gate
  and u_sb (sb, Op[5], ~Op[4], Op[3], ~Op[2], ~Op[1], ~Op[0]);  // AND_Gate
  and addu (addu_out, ~Op[5], ~Op[4], ~Op[3], ~Op[2], ~Op[1], ~Op[0], Func[5], ~Func[4], ~Func[3], ~Func[2], ~Func[1], Func[0]);  // AND_Gate
  and subu (subu_out, ~Op[5], ~Op[4], ~Op[3], ~Op[2], ~Op[1], ~Op[0], Func[5], ~Func[4], ~Func[3], ~Func[2], Func[1], Func[0]);  // AND_Gate
  and ori (ori_out, ~Op[5], ~Op[4], Op[3], Op[2], ~Op[1], Op[0]);  // AND_Gate
  and addiu (addiu_out, ~Op[5], ~Op[4], Op[3], ~Op[2], ~Op[1], Op[0]);  // AND_Gate
  and lui (lui_out, ~Op[5], ~Op[4], Op[3], Op[2], Op[1], Op[0]);  // AND_Gate
  and beq (b_beq, ~Op[5], ~Op[4], ~Op[3], Op[2], ~Op[1], ~Op[0]);  // AND_Gate
  and bgtz (b_bgtz, ~Op[5], ~Op[4], ~Op[3], Op[2], Op[1], Op[0]);  // AND_Gate
  and j (j_out, ~Op[5], ~Op[4], ~Op[3], ~Op[2], Op[1], ~Op[0]);  // AND_Gate
  and jal (jal_out, ~Op[5], ~Op[4], ~Op[3], ~Op[2], Op[1], Op[0]);  // AND_Gate
  and jr (b_jr, ~Op[5], ~Op[4], ~Op[3], ~Op[2], ~Op[1], ~Op[0], ~Func[5], ~Func[4], Func[3], ~Func[2], ~Func[1], ~Func[0]);  // AND_Gate
  buf or_1 (EXTOp[1], ori_out);  // OR_Gate
  buf or_2 (EXTOp[0], lui_out);  // OR_Gate
  or or_3 (ALUOp[2], subu_out, b_beq);
  or or_4 (ALUOp[1], lw_out, lb, sw_out, sb, addu_out, addiu_out);
  or or_5 (ALUOp[0], ori_out, lui_out);
  or or_6 (ALUSrc, addu_out, subu_out, b_beq);
  buf or_7 (RegDst[1], jal_out);  // OR_Gate
  or or_8 (RegDst[0], addu_out, subu_out);
  or or_9 (RegSrc[1], lui_out, jal_out);
  or or_10 (RegSrc[0], addu_out, subu_out, ori_out, addiu_out, jal_out);
  or or_11 (RegWrite, lw_out, lb, addu_out, subu_out, ori_out, addiu_out, lui_out, jal_out);
  or or_12 (MemRead, lw_out, lb, sb);
  or or_13 (MemWrite, sw_out, sb);
  or or_14 (b_j_jal, j_out, jal_out);

  assign ALUOp[3] = 1'b0;
endmodule

module EXT (
  input  [1:0] EXT_Op,
  input  [15:0] Input_16,
  output [31:0] Output_32
);

  wire [31:0] bit_extender_1_out, bit_extender_2_out;

  assign bit_extender_1_out = {{16{Input_16[15]}}, Input_16};  // Bit_Extender bit_extender_1
  assign bit_extender_2_out = {{16{1'b0}}, Input_16};  // Bit_Extender bit_extender_2
  Multiplexer #(.select(2), .width(32), .enable("false")) multiplexer_1 (
    .in0(bit_extender_1_out), .in1({Input_16, {16{1'b0}}}), .in2(bit_extender_2_out), .out(Output_32),
    .sel(EXT_Op));  // open: in3
endmodule

module ALU (
  input  [31:0] A,
  input  [31:0] B,
  input  [3:0] ALUOp,
  output out_4,
  output [31:0] out_5
);

  wire [31:0] adder_1_out, and_1_out, or_1_out, subtractor_1_out;

  assign and_1_out = B & A;  // AND_Gate and_1, 32 bits wide
  assign or_1_out = B | A;  // OR_Gate or_1, 32 bits wide
  Adder #(.width(32)) adder_1 (.a(A), .b(B), .out(adder_1_out));  // open: cin, cout
  Subtractor #(.width(32)) subtractor_1 (.a(A), .b(B), .out(subtractor_1_out));  // open: bin, bout
  Multiplexer #(.select(4), .width(32), .enable("false")) multiplexer_1 (
    .in0(and_1_out), .in1(or_1_out), .in2(adder_1_out), .in4(subtractor_1_out), .out(out_5), .sel(ALUOp));  // open: in3, in5, in6, in7, in8, in9, in10, in11, in12, in13, in14, in15
  Comparator #(.width(32)) comparator_1 (.a({32{1'b0}}), .b(out_5), .eq(out_4));  // open: gt, lt
endmodule

module DM (
  input  lb,
  input  in_2,
  input  reset,
  input  sb,
  input  [31:0] in_5,
  input  [31:0] in_6,
  input  MemW,
  input  MemR,
  output [31:0] RD
);

  wire or_1_out, pull_resistor_1_node;
  wire [31:0] bit_extender_1_out, bit_extender_2_out, bit_extender_3_out, bit_extender_4_out, lb_data,
       multiplexer_1_out, out_word, sb_data;

  Multiplexer #(.width(32), .enable("false")) multiplexer_1 (
    .in0(in_6), .in1(sb_data), .out(multiplexer_1_out), .sel(sb));
  assign bit_extender_1_out = {{24{1'b0}}, out_word[7:0]};  // Bit_Extender bit_extender_1
  assign bit_extender_2_out = {{24{1'b0}}, out_word[15:8]};  // Bit_Extender bit_extender_2
  assign bit_extender_3_out = {{24{1'b0}}, out_word[23:16]};  // Bit_Extender bit_extender_3
  assign bit_extender_4_out = {{24{1'b0}}, out_word[31:24]};  // Bit_Extender bit_extender_4
  or or_1 (or_1_out, MemR, pull_resistor_1_node);
  Pull_Resistor #(.pull(1)) pull_resistor_1 (.node(pull_resistor_1_node));
  RAM #(.addrWidth(5), .dataWidth(32), .bus("separate")) ram_1 (
    .addr(in_5[6:2]), .din(multiplexer_1_out), .data(out_word), .str(MemW), .clk(in_2), .ld(or_1_out),
    .clr(reset));  // open: sel
  Multiplexer #(.select(2), .width(32), .enable("false")) multiplexer_2 (
    .in0(bit_extender_1_out), .in1(bit_extender_2_out), .in2(bit_extender_3_out), .in3(bit_extender_4_out),
    .out(lb_data), .sel(in_5[1:0]));
  Multiplexer #(.select(2), .width(32), .enable("false")) multiplexer_3 (
    .in0({out_word[31:8], in_6[7:0]}), .in1({out_word[31:16], in_6[7:0], out_word[7:0]}),
    .in2({out_word[31:24], in_6[7:0], out_word[15:0]}), .in3({in_6[7:0], out_word[23:0]}), .out(sb_data),
    .sel(in_5[1:0]));
  Multiplexer #(.width(32), .enable("false")) multiplexer_4 (.in0(out_word), .in1(lb_data), .out(RD), .sel(lb));

  // Other names for the same wires on the sheet: in_word[31:0] = in_6; Clk_prime = in_2; Offs[1:0] = in_5[1:0]
endmodule
