// Logisim project CPU.circ as structural Verilog: 25 circuits, main circuit main
module main (
  input  in_1,
  output [31:0] out_2,
  output Reg_Write,
  output [4:0] out_4,
  output [31:0] Reg_Data,
  output MemWrite,
  output [4:0] out_7,
  output [31:0] Mem_Data
);

  wire ALU_Src, b_beq, b_bgtz, b_j_jal, b_jr, Clk_prime, comparator_1_eq, ctrl_m_1_lb, ctrl_m_1_rm,
       ctrl_m_1_sb, forwardunit_1_frtmsel, MR, StallD, StallE, StallF;
  wire [1:0] Ctrl_D_extop, ctrl_e_1_reg_dst, ctrl_w_1_wd_op, forwardunit_1_frsdsel, forwardunit_1_frsesel,
       forwardunit_1_frtdsel, forwardunit_1_frtesel, sf_d_1_tuse1_d, sf_d_1_tuse2_d;
  wire [3:0] ctrl_e_1_aluctrl, sf_e_1_tnew_e, sf_m_1_tnew_m, sf_w_1_tnew_w;
  wire [4:0] multiplexer_3_out, rd_D, Reg_DE_rd_o, Reg_DE_rt_o, Reg_EM_out_12, rs_D, rt_D, sf_d_1_s1_d,
       sf_d_1_s2_d, sf_e_1_des_e, sf_e_1_s1_e, sf_e_1_s2_e, sf_m_1_des_m, sf_m_1_s2_m, sf_w_1_des_w;
  wire [5:0] splitter_1_func, splitter_1_op;
  wire [9:0] addtorom_1_output_10;
  wire [15:0] splitter_1_imm_16;
  wire [25:0] imm_26;
  wire [31:0] alu_1_out_4, aluresult_E, aluresult_W, D_CMP_RS, D_CMP_RT, dm_1_rd, E_ALU_A, E_ALU_B, etod,
       ext, inst_D, inst_E, inst_M, inst_W, M_DM_WD, MemAdd, mtod, multiplexer_2_out, npc, pc_1_output,
       pc_4_D, pc_8_D, pc_8_E, pc_8_M, pc_8_W, pc_D, rd1, rd2, readdatd_W, Reg_DE_out_22, Reg_DE_pc_4_o,
       Reg_DE_pc_o, Reg_EM_pc_4_o, Reg_EM_pc_o, rs_e, rt_e, writedata_M, wtod;

  Clock clock_1 (.out(Clk_prime));
  PC pc_1 (.Input(npc), .Output(pc_1_output), .Reset(in_1), .CLK(Clk_prime), .StallF(StallF));
  // Probe on pc_1_output
  ADDtoROM addtorom_1 (.Input_32(pc_1_output), .Output_10(addtorom_1_output_10));
  // Probe on out_2
  ROM #(.addrWidth(10), .dataWidth(32)) rom_1 (.addr(addtorom_1_output_10), .data(out_2));  // open: sel
  Reg_FD reg_fd_1 (
    .instr_i(out_2), .pc_i(pc_1_output), .instr_o(inst_D), .pc_o(pc_D), .pc_o_2(pc_4_D), .pc_o_3(pc_8_D),
    .in_1(Clk_prime), .in_2(in_1), .in_5(StallD));
  NPC npc_1 (
    .pc(pc_1_output), .imm_26(imm_26), .RD1(D_CMP_RS), .equal(comparator_1_eq), .npc(npc), .beq(b_beq),
    .j_jal(b_j_jal), .jr(b_jr), .bgtz(b_bgtz));
  splitter splitter_1 (
    .inst(inst_D), .Op(splitter_1_op), .Func(splitter_1_func), .rs(rs_D), .rt(rt_D), .rd(rd_D),
    .imm_16(splitter_1_imm_16), .add_26(imm_26));  // open: shamt
  Comparator #(.width(32)) comparator_1 (.a(D_CMP_RS), .b(D_CMP_RT), .eq(comparator_1_eq));  // open: gt, lt
  ctrl_D Ctrl_D (
    .OP(splitter_1_op), .Func(splitter_1_func), .b_j_jal(b_j_jal), .b_beq(b_beq), .b_jr(b_jr),
    .EXTOp(Ctrl_D_extop), .b_bgtz(b_bgtz));
  EXT ext_1 (.Input_16(splitter_1_imm_16), .Output_32(ext), .EXT_Op(Ctrl_D_extop));
  // Probe on ext
  GRF grf_1 (
    .A1(rs_D), .A2(rt_D), .A3(out_4), .WD(Reg_Data), .RD1(rd1), .RD2(rd2), .clk(Clk_prime), .reset(in_1),
    .we(Reg_Write));
  SF_D sf_d_1 (
    .s1_D(sf_d_1_s1_d), .s2_D(sf_d_1_s2_d), .Inst(inst_D), .tuse1_D(sf_d_1_tuse1_d), .tuse2_D(sf_d_1_tuse2_d));
  SF_E sf_e_1 (
    .pc_8(pc_8_E), .des_E(sf_e_1_des_e), .s1_E(sf_e_1_s1_e), .s2_E(sf_e_1_s2_e), .tnew_E(sf_e_1_tnew_e),
    .EtoD(etod), .Inst(inst_E), .ext_E(ext));  // open: tuse1_E, tuse2_E
  SF_M sf_m_1 (
    .ALUOut(aluresult_E), .pc_8(pc_8_M), .des_M(sf_m_1_des_m), .s2_M(sf_m_1_s2_m), .tnew_M(sf_m_1_tnew_m),
    .MtoD(mtod), .Inst(inst_M));  // open: tuse2_M
  SF_W sf_w_1 (
    .aluresult(aluresult_W), .pc_8(pc_8_W), .readData(readdatd_W), .des_W(sf_w_1_des_w),
    .tnew_W(sf_w_1_tnew_w), .WtoD(wtod), .Inst(inst_W));
  // Probe on multiplexer_2_out
  stallUnit stallunit_1 (
    .s1_D(sf_d_1_s1_d), .s2_D(sf_d_1_s2_d), .tUse1_D(sf_d_1_tuse1_d), .tUse2_D(sf_d_1_tuse2_d),
    .des_E(sf_e_1_des_e), .tNew_E(sf_e_1_tnew_e), .tNew_M(sf_m_1_tnew_m), .des_M(sf_m_1_des_m),
    .Stall_F(StallF), .Stall_D(StallD), .flush_E(StallE));
  Reg_DE Reg_DE (
    .pc_i(pc_D), .RD1_i(D_CMP_RS), .pc_4_i(pc_4_D), .RD2_i(D_CMP_RT), .pc_8_i(pc_8_D), .rs_i(rs_D),
    .rt_i(rt_D), .rd_i(rd_D), .instr_i(inst_D), .pc_o(Reg_DE_pc_o), .RD1_o(rs_e), .pc_4_o(Reg_DE_pc_4_o),
    .RD2_o(rt_e), .pc_8_o(pc_8_E), .rt_o(Reg_DE_rt_o), .rd_o(Reg_DE_rd_o), .out_23(inst_E), .in_1(Clk_prime),
    .in_2(in_1), .in_13(StallE), .out_22(Reg_DE_out_22), .extresult_i(ext));  // open: rs_o
  Multiplexer #(.select(2), .width(32), .enable("false")) multiplexer_1 (
    .in0(rd1), .in1(etod), .in2(mtod), .in3({32{1'b0}}), .out(D_CMP_RS), .sel(forwardunit_1_frsdsel));
  // Probe on E_ALU_A
  Multiplexer #(.width(32), .enable("false")) multiplexer_2 (
    .in0(Reg_DE_out_22), .in1(E_ALU_B), .out(multiplexer_2_out), .sel(ALU_Src));
  Ctrl_E ctrl_e_1 (
    .OP(inst_E[31:26]), .Func(inst_E[5:0]), .Reg_Dst(ctrl_e_1_reg_dst), .ALUCtrl(ctrl_e_1_aluctrl),
    .ALUSrc(ALU_Src));
  Multiplexer #(.select(2), .width(5), .enable("false")) multiplexer_3 (
    .in0(Reg_DE_rt_o), .in1(Reg_DE_rd_o), .in2({5{1'b1}}), .out(multiplexer_3_out), .sel(ctrl_e_1_reg_dst));  // open: in3
  Multiplexer #(.select(2), .width(32), .enable("false")) multiplexer_4 (
    .in0(rd2), .in1(etod), .in2(mtod), .in3({32{1'b0}}), .out(D_CMP_RT), .sel(forwardunit_1_frtdsel));
  ALU alu_1 (.A(E_ALU_A), .B(multiplexer_2_out), .ALUOp(ctrl_e_1_aluctrl), .out_4(alu_1_out_4));
  forwardUnit forwardunit_1 (
    .s1_D(sf_d_1_s1_d), .s2_D(sf_d_1_s2_d), .s1_E(sf_e_1_s1_e), .s2_E(sf_e_1_s2_e), .des_E(sf_e_1_des_e),
    .tNew_E(sf_e_1_tnew_e), .s2_M(sf_m_1_s2_m), .tNew_M(sf_m_1_tnew_m), .des_M(sf_m_1_des_m),
    .tNew_W(sf_w_1_tnew_w), .des_W(sf_w_1_des_w), .fRsDsel(forwardunit_1_frsdsel),
    .fRtDsel(forwardunit_1_frtdsel), .fRsEsel(forwardunit_1_frsesel), .fRtEsel(forwardunit_1_frtesel),
    .fRtMsel(forwardunit_1_frtmsel));
  // Probe on alu_1_out_4
  Reg_EM Reg_EM (
    .aluresult_i(alu_1_out_4), .writedata_i(E_ALU_B), .writereg_i(multiplexer_3_out), .pc_i(Reg_DE_pc_o),
    .pc_4_i(Reg_DE_pc_4_o), .pc_8_i(pc_8_E), .instr_i(inst_E), .out_10(aluresult_E), .out_11(writedata_M),
    .out_12(Reg_EM_out_12), .pc_o(Reg_EM_pc_o), .pc_4_o(Reg_EM_pc_4_o), .pc_8_o(pc_8_M), .out_16(inst_M),
    .in_1(Clk_prime), .in_2(in_1));
  Multiplexer #(.select(2), .width(32), .enable("false")) multiplexer_5 (
    .in0(rs_e), .in1(mtod), .in2(wtod), .in3({32{1'b0}}), .out(E_ALU_A), .sel(forwardunit_1_frsesel));
  // Probe on aluresult_E
  Ctrl_M ctrl_m_1 (
    .OP(inst_M[31:26]), .Func(inst_M[5:0]), .WM(MR), .RM(ctrl_m_1_rm), .lb(ctrl_m_1_lb), .sb(ctrl_m_1_sb));
  // Probe on writedata_M
  // Probe on forwardunit_1_frtesel
  Multiplexer #(.select(2), .width(32), .enable("false")) multiplexer_6 (
    .in0(rt_e), .in1(mtod), .in2(wtod), .in3({32{1'b0}}), .out(E_ALU_B), .sel(forwardunit_1_frtesel));
  DM dm_1 (
    .in_5(aluresult_E), .in_6(M_DM_WD), .RD(dm_1_rd), .in_2(Clk_prime), .reset(in_1), .MemW(MR),
    .MemR(ctrl_m_1_rm), .lb(ctrl_m_1_lb), .sb(ctrl_m_1_sb));
  Multiplexer #(.width(32), .enable("false")) multiplexer_7 (
    .in0(writedata_M), .in1(wtod), .out(M_DM_WD), .sel(forwardunit_1_frtmsel));
  REG_MW Reg_MW (
    .writereg_i(Reg_EM_out_12), .aluresult_i(aluresult_E), .writedata_i(writedata_M), .readdata_i(dm_1_rd),
    .pc_i(Reg_EM_pc_o), .pc_4_i(Reg_EM_pc_4_o), .pc_8_i(pc_8_M), .instr_i(inst_M), .memaddr(aluresult_E),
    .memdata(M_DM_WD), .memwrite(MR), .out_14(out_4), .out_15(aluresult_W), .out_17(readdatd_W),
    .pc_8_o(pc_8_W), .out_21(inst_W), .out_22({MemAdd[31:7], out_7, MemAdd[1:0]}), .out_23(Mem_Data),
    .out_24(MemWrite), .in_1(Clk_prime), .in_2(in_1));  // open: out_16, pc_o, pc_4_o
  Ctrl_W ctrl_w_1 (.OP(inst_W[31:26]), .Func(inst_W[5:0]), .WriteReg(Reg_Write), .WD_Op(ctrl_w_1_wd_op));
  Multiplexer #(.select(2), .width(32), .enable("false")) multiplexer_8 (
    .in1(aluresult_W), .in2(pc_8_W), .in3(readdatd_W), .out(Reg_Data), .sel(ctrl_w_1_wd_op));  // open: in0

  // Other names for the same wires on the sheet: instr[31:0] = out_2; MemAdd[6:2] = out_7; MemData[31:0] = Mem_Data;
  //   Reset = in_1; WR = Reg_Write; WriteReg[4:0] = out_4

  // Notes on the sheet:
  //   0:ext  1:ALUOut  2:pc+8  3:RD
endmodule

module splitter (
  input  [31:0] inst,
  output [5:0] Op,
  output [5:0] Func,
  output [4:0] rs,
  output [4:0] rt,
  output [4:0] rd,
  output [15:0] imm_16,
  output [25:0] add_26,
  output [4:0] shamt
);


  assign add_26 = inst[25:0];
  assign Func = inst[5:0];
  assign imm_16 = inst[15:0];
  assign Op = inst[31:26];
  assign rd = inst[15:11];
  assign rs = inst[25:21];
  assign rt = inst[20:16];
  assign shamt = inst[10:6];
endmodule

// 32-5
module ADDtoROM (
  input  [31:0] Input_32,
  output [9:0] Output_10
);

  wire [31:0] subtractor_1_out;

  Subtractor #(.width(32)) subtractor_1 (
    .a(Input_32), .b(32'h3000), .out({subtractor_1_out[31:12], Output_10, subtractor_1_out[1:0]}));  // open: bin, bout
endmodule

module PC (
  input  [31:0] Input,
  input  Reset,
  input  CLK,
  input  StallF,
  output [31:0] Output
);

  wire not_1_out;
  wire [31:0] multiplexer_1_out;

  Multiplexer #(.width(32), .enable("false")) multiplexer_1 (
    .in0(Input), .in1(32'h3000), .out(multiplexer_1_out), .sel(Reset));
  Register #(.width(32)) register_1 (.D(multiplexer_1_out), .en(not_1_out), .Q(Output), .clk(CLK));  // open: clr
  not not_1 (not_1_out, StallF);
endmodule

module NPC (
  input  beq,
  input  j_jal,
  input  jr,
  input  bgtz,
  input  equal,
  input  [31:0] pc,
  input  [25:0] imm_26,
  input  [31:0] RD1,
  output [31:0] npc
);

  wire and_1_out, and_2_out, comparator_1_gt;
  wire [1:0] NPCOp;
  wire [27:0] bit_extender_2_out, n2_28_1_out_2;
  wire [31:0] adder_1_out, adder_2_out, bit_extender_1_out, n2_32_1_out_2;

  Adder #(.width(32)) adder_1 (.a(32'h4), .b(pc), .out(adder_1_out));  // open: cin, cout
  assign bit_extender_1_out = {{16{imm_26[15]}}, imm_26[15:0]};  // Bit_Extender bit_extender_1
  assign bit_extender_2_out = {{2{imm_26[25]}}, imm_26};  // Bit_Extender bit_extender_2
  _2_32 u_2_32_1 (.in_1(bit_extender_1_out), .out_2(n2_32_1_out_2));
  _2_28 u_2_28_1 (.in_1(bit_extender_2_out), .out_2(n2_28_1_out_2));
  Adder #(.width(32)) adder_2 (.a(pc), .b(n2_32_1_out_2), .out(adder_2_out));  // open: cin, cout
  // Probe on adder_1_out
  Multiplexer #(.select(2), .width(32), .enable("false")) multiplexer_1 (
    .in0(adder_1_out), .in1(adder_2_out), .in2({pc[31:28], n2_28_1_out_2}), .in3(RD1), .out(npc), .sel(NPCOp));
  and and_1 (and_1_out, beq, equal);
  Comparator #(.width(32)) comparator_1 (.a(RD1), .b({32{1'b0}}), .gt(comparator_1_gt));  // open: eq, lt
  or or_1 (NPCOp[0], jr, and_1_out, and_2_out);
  and and_2 (and_2_out, bgtz, comparator_1_gt);
  or or_2 (NPCOp[1], j_jal, jr);
endmodule

module _2_28 (
  input  [27:0] in_1,
  output [27:0] out_2
);

  Shifter #(.width(28)) shifter_1 (.in(in_1), .\dist (5'b00010), .out(out_2));
endmodule

module _2_32 (
  input  [31:0] in_1,
  output [31:0] out_2
);

  Shifter #(.width(32)) shifter_1 (.in(in_1), .\dist (5'b00010), .out(out_2));
endmodule

module EXT (
  input  [1:0] EXT_Op,
  input  [15:0] Input_16,
  output [31:0] Output_32
);

  wire [31:0] bit_extender_1_out, bit_extender_2_out;

  assign bit_extender_1_out = {{16{Input_16[15]}}, Input_16};  // Bit_Extender bit_extender_1
  assign bit_extender_2_out = {{16{1'b0}}, Input_16};  // Bit_Extender bit_extender_2
  Multiplexer #(.select(2), .width(32), .enable("false")) multiplexer_1 (
    .in0(bit_extender_1_out), .in1({Input_16, {16{1'b0}}}), .in2(bit_extender_2_out), .out(Output_32),
    .sel(EXT_Op));  // open: in3
endmodule

module ctrl_D (
  input  [5:0] OP,
  input  [5:0] Func,
  output b_j_jal,
  output b_beq,
  output b_jr,
  output b_bgtz,
  output [1:0] EXTOp
);

  wire j_out, jal_out;

  // AND_Gate lw has open pins: in0=OP[5], in1=OP[4], in2=OP[3], in3=OP[2], in4=OP[1], in5=OP[0], out=open
  // AND_Gate sw has open pins: in0=OP[5], in1=OP[4], in2=OP[3], in3=OP[2], in4=OP[1], in5=OP[0], out=open
  // AND_Gate addu has open pins: in0=OP[5], in1=OP[4], in2=OP[3], in3=OP[2], in4=OP[1], in5=OP[0], in6=Func[5], in7=Func[4], in8=Func[3], in9=Func[2], in10=Func[1], in11=Func[0], out=open
  // AND_Gate subu has open pins: in0=OP[5], in1=OP[4], in2=OP[3], in3=OP[2], in4=OP[1], in5=OP[0], in6=Func[5], in7=Func[4], in8=Func[3], in9=Func[2], in10=Func[1], in11=Func[0], out=open
  and ori (EXTOp[1], ~OP[5], ~OP[4], OP[3], OP[2], ~OP[1], OP[0]);  // AND_Gate
  // AND_Gate addui has open pins: in0=OP[5], in1=OP[4], in2=OP[3], in3=OP[2], in4=OP[1], in5=OP[0], out=open
  and lui (EXTOp[0], ~OP[5], ~OP[4], OP[3], OP[2], OP[1], OP[0]);  // AND_Gate
  and jal (jal_out, ~OP[5], ~OP[4], ~OP[3], ~OP[2], OP[1], OP[0]);  // AND_Gate
  and j (j_out, ~OP[5], ~OP[4], ~OP[3], ~OP[2], OP[1], ~OP[0]);  // AND_Gate
  and beq (b_beq, ~OP[5], ~OP[4], ~OP[3], OP[2], ~OP[1], ~OP[0]);  // AND_Gate
  and jr (b_jr, ~OP[5], ~OP[4], ~OP[3], ~OP[2], ~OP[1], ~OP[0], ~Func[5], ~Func[4], Func[3], ~Func[2], ~Func[1], ~Func[0]);  // AND_Gate
  and bgtz (b_bgtz, ~OP[5], ~OP[4], ~OP[3], OP[2], OP[1], OP[0]);  // AND_Gate
  // AND_Gate lb has open pins: in0=OP[5], in1=OP[4], in2=OP[3], in3=OP[2], in4=OP[1], in5=OP[0], out=open
  // AND_Gate sb has open pins: in0=OP[5], in1=OP[4], in2=OP[3], in3=OP[2], in4=OP[1], in5=OP[0], out=open
  or or_1 (b_j_jal, j_out, jal_out);
endmodule

module Reg_FD (
  input  in_1,
  input  in_2,
  input  [31:0] instr_i,
  input  [31:0] pc_i,
  input  in_5,
  output [31:0] instr_o,
  output [31:0] pc_o,
  output [31:0] pc_o_2,
  output [31:0] pc_o_3
);

  wire clk_prime, not_1_out, not_2_out;

  not not_1 (not_1_out, in_5);
  not not_2 (not_2_out, in_5);
  buf and_1 (clk_prime, in_1);  // AND_Gate
  Register #(.width(32)) register_1 (.D(instr_i), .en(not_1_out), .Q(instr_o), .clk(clk_prime), .clr(in_2));
  Register #(.width(32)) register_2 (.D(pc_i), .en(not_2_out), .Q(pc_o), .clk(clk_prime), .clr(in_2));
  Adder #(.width(32)) adder_1 (.a(pc_o), .b(32'h4), .out(pc_o_2));  // open: cin, cout
  Adder #(.width(32)) adder_2 (.a(pc_o), .b(32'h8), .out(pc_o_3));  // open: cin, cout

  // Other names for the same wires on the sheet: clk = in_1; F_D_stall = in_5; reset = in_2
endmodule

module GRF (
  input  [4:0] A1,
  input  clk,
  input  reset,
  input  we,
  input  [4:0] A2,
  input  [4:0] A3,
  input  [31:0] WD,
  output [31:0] RD1,
  output [31:0] RD2
);

  wire and_1_out, and_2_out, CLK_t, comparator_1_eq, comparator_2_eq, comparator_3_eq, comparator_4_eq,
       not_2_out, not_3_out;
  wire [31:0] I0, I1, I2, I3, I4, I5, I6, I7, I8, I9, I10, I11, I12, I13, I14, I15, I16, I17, I18, I19, I20,
       I21, I22, I23, I24, I25, I26, I27, I28, I29, I30, I31, O0, O1, O2, O3, O4, O5, O6, O7, O8, O9, O10,
       O11, O12, O13, O14, O15, O16, O17, O18, O19, O20, O21, O22, O23, O24, O25, O26, O27, O28, O29, O30,
       O31, RD1_t, RD2_t;

  Demultiplexer #(.select(5), .width(32), .tristate("true")) demultiplexer_1 (
    .out0(I0), .out1(I1), .out2(I2), .out3(I3), .out4(I4), .out5(I5), .out6(I6), .out7(I7), .out8(I8),
    .out9(I9), .out10(I10), .out11(I11), .out12(I12), .out13(I13), .out14(I14), .out15(I15), .out16(I16),
    .out17(I17), .out18(I18), .out19(I19), .out20(I20), .out21(I21), .out22(I22), .out23(I23), .out24(I24),
    .out25(I25), .out26(I26), .out27(I27), .out28(I28), .out29(I29), .out30(I30), .out31(I31), .in(WD),
    .sel(A3));  // open: en
  not not_1 (CLK_t, clk);
  Comparator #(.width(5)) comparator_1 (.a(A3), .b(A1), .eq(comparator_1_eq));  // open: gt, lt
  Comparator #(.width(5)) comparator_2 (.a(A1), .b({5{1'b0}}), .eq(comparator_2_eq));  // open: gt, lt
  Comparator #(.width(5)) comparator_3 (.a(A3), .b(A2), .eq(comparator_3_eq));  // open: gt, lt
  Comparator #(.width(5)) comparator_4 (.a(A2), .b({5{1'b0}}), .eq(comparator_4_eq));  // open: gt, lt
  not not_2 (not_2_out, comparator_2_eq);
  not not_3 (not_3_out, comparator_4_eq);
  Multiplexer #(.select(5), .width(32)) multiplexer_1 (
    .in0(O0), .in1(O1), .in2(O2), .in3(O3), .in4(O4), .in5(O5), .in6(O6), .in7(O7), .in8(O8), .in9(O9),
    .in10(O10), .in11(O11), .in12(O12), .in13(O13), .in14(O14), .in15(O15), .in16(O16), .in17(O17),
    .in18(O18), .in19(O19), .in20(O20), .in21(O21), .in22(O22), .in23(O23), .in24(O24), .in25(O25),
    .in26(O26), .in27(O27), .in28(O28), .in29(O29), .in30(O30), .in31(O31), .out(RD2_t), .sel(A2));  // open: en
  Multiplexer #(.width(32), .enable("false")) multiplexer_2 (.in0(RD1_t), .in1(WD), .out(RD1), .sel(1'b0));
  and and_1 (and_1_out, comparator_1_eq, not_2_out);
  Multiplexer #(.width(32), .enable("false")) multiplexer_3 (.in0(RD2_t), .in1(WD), .out(RD2), .sel(1'b0));
  and and_2 (and_2_out, comparator_3_eq, not_3_out);
  Multiplexer #(.select(5), .width(32)) multiplexer_4 (
    .in0(O0), .in1(O1), .in2(O2), .in3(O3), .in4(O4), .in5(O5), .in6(O6), .in7(O7), .in8(O8), .in9(O9),
    .in10(O10), .in11(O11), .in12(O12), .in13(O13), .in14(O14), .in15(O15), .in16(O16), .in17(O17),
    .in18(O18), .in19(O19), .in20(O20), .in21(O21), .in22(O22), .in23(O23), .in24(O24), .in25(O25),
    .in26(O26), .in27(O27), .in28(O28), .in29(O29), .in30(O30), .in31(O31), .out(RD1_t), .sel(A1));  // open: en
  Register #(.width(32)) register_1 (.D({32{1'b0}}), .en(we), .Q(O0), .clk(CLK_t), .clr(reset));
  Register #(.width(32)) register_2 (.D(I8), .en(we), .Q(O8), .clk(CLK_t), .clr(reset));
  Register #(.width(32)) register_3 (.D(I16), .en(we), .Q(O16), .clk(CLK_t), .clr(reset));
  Register #(.width(32)) register_4 (.D(I24), .en(we), .Q(O24), .clk(CLK_t), .clr(reset));
  Register #(.width(32)) register_5 (.D(I1), .en(we), .Q(O1), .clk(CLK_t), .clr(reset));
  Register #(.width(32)) register_6 (.D(I9), .en(we), .Q(O9), .clk(CLK_t), .clr(reset));
  Register #(.width(32)) register_7 (.D(I17), .en(we), .Q(O17), .clk(CLK_t), .clr(reset));
  Register #(.width(32)) register_8 (.D(I25), .en(we), .Q(O25), .clk(CLK_t), .clr(reset));
  Register #(.width(32)) register_9 (.D(I2), .en(we), .Q(O2), .clk(CLK_t), .clr(reset));
  Register #(.width(32)) register_10 (.D(I10), .en(we), .Q(O10), .clk(CLK_t), .clr(reset));
  Register #(.width(32)) register_11 (.D(I18), .en(we), .Q(O18), .clk(CLK_t), .clr(reset));
  Register #(.width(32)) register_12 (.D(I26), .en(we), .Q(O26), .clk(CLK_t), .clr(reset));
  Register #(.width(32)) register_13 (.D(I3), .en(we), .Q(O3), .clk(CLK_t), .clr(reset));
  Register #(.width(32)) register_14 (.D(I11), .en(we), .Q(O11), .clk(CLK_t), .clr(reset));
  Register #(.width(32)) register_15 (.D(I19), .en(we), .Q(O19), .clk(CLK_t), .clr(reset));
  Register #(.width(32)) register_16 (.D(I27), .en(we), .Q(O27), .clk(CLK_t), .clr(reset));
  Register #(.width(32)) register_17 (.D(I4), .en(we), .Q(O4), .clk(CLK_t), .clr(reset));
  Register #(.width(32)) register_18 (.D(I12), .en(we), .Q(O12), .clk(CLK_t), .clr(reset));
  Register #(.width(32)) register_19 (.D(I20), .en(we), .Q(O20), .clk(CLK_t), .clr(reset));
  Register #(.width(32)) register_20 (.D(I28), .en(we), .Q(O28), .clk(CLK_t), .clr(reset));
  Register #(.width(32)) register_21 (.D(I5), .en(we), .Q(O5), .clk(CLK_t), .clr(reset));
  Register #(.width(32)) register_22 (.D(I13), .en(we), .Q(O13), .clk(CLK_t), .clr(reset));
  Register #(.width(32)) register_23 (.D(I21), .en(we), .Q(O21), .clk(CLK_t), .clr(reset));
  Register #(.width(32)) register_24 (.D(I29), .en(we), .Q(O29), .clk(CLK_t), .clr(reset));
  Register #(.width(32)) register_25 (.D(I6), .en(we), .Q(O6), .clk(CLK_t), .clr(reset));
  Register #(.width(32)) register_26 (.D(I14), .en(we), .Q(O14), .clk(CLK_t), .clr(reset));
  Register #(.width(32)) register_27 (.D(I22), .en(we), .Q(O22), .clk(CLK_t), .clr(reset));
  Register #(.width(32)) register_28 (.D(I30), .en(we), .Q(O30), .clk(CLK_t), .clr(reset));
  Register #(.width(32)) register_29 (.D(I7), .en(we), .Q(O7), .clk(CLK_t), .clr(reset));
  Register #(.width(32)) register_30 (.D(I15), .en(we), .Q(O15), .clk(CLK_t), .clr(reset));
  Register #(.width(32)) register_31 (.D(I23), .en(we), .Q(O23), .clk(CLK_t), .clr(reset));
  Register #(.width(32)) register_32 (.D(I31), .en(we), .Q(O31), .clk(CLK_t), .clr(reset));
endmodule

module Reg_DE (
  input  in_1,
  input  in_2,
  input  [31:0] pc_i,
  input  [31:0] RD1_i,
  input  [31:0] pc_4_i,
  input  [31:0] RD2_i,
  input  [31:0] pc_8_i,
  input  [4:0] rs_i,
  input  [4:0] rt_i,
  input  [4:0] rd_i,
  input  [31:0] extresult_i,
  input  [31:0] instr_i,
  input  in_13,
  output [31:0] pc_o,
  output [31:0] RD1_o,
  output [31:0] pc_4_o,
  output [31:0] RD2_o,
  output [31:0] pc_8_o,
  output [4:0] rs_o,
  output [4:0] rt_o,
  output [4:0] rd_o,
  output [31:0] out_22,
  output [31:0] out_23
);

  wire [4:0] multiplexer_3_out, multiplexer_4_out, multiplexer_5_out;
  wire [31:0] multiplexer_1_out, multiplexer_2_out, multiplexer_6_out, multiplexer_7_out, multiplexer_8_out,
       multiplexer_9_out, multiplexer_10_out;

  Multiplexer #(.width(32), .enable("false")) multiplexer_1 (
    .in0(RD1_i), .in1({32{1'b0}}), .out(multiplexer_1_out), .sel(in_13));
  Multiplexer #(.width(32), .enable("false")) multiplexer_2 (
    .in0(RD2_i), .in1({32{1'b0}}), .out(multiplexer_2_out), .sel(in_13));
  Multiplexer #(.width(5), .enable("false")) multiplexer_3 (
    .in0(rs_i), .in1({5{1'b0}}), .out(multiplexer_3_out), .sel(in_13));
  Multiplexer #(.width(5), .enable("false")) multiplexer_4 (
    .in0(rt_i), .in1({5{1'b0}}), .out(multiplexer_4_out), .sel(in_13));
  Multiplexer #(.width(5), .enable("false")) multiplexer_5 (
    .in0(rd_i), .in1({5{1'b0}}), .out(multiplexer_5_out), .sel(in_13));
  Multiplexer #(.width(32), .enable("false")) multiplexer_6 (
    .in0(extresult_i), .in1({32{1'b0}}), .out(multiplexer_6_out), .sel(in_13));
  Multiplexer #(.width(32), .enable("false")) multiplexer_7 (
    .in0(instr_i), .in1({32{1'b0}}), .out(multiplexer_7_out), .sel(in_13));
  Register #(.width(32)) register_1 (.D(multiplexer_1_out), .Q(RD1_o), .clk(in_1), .clr(in_2));  // open: en
  Register #(.width(32)) register_2 (.D(multiplexer_2_out), .Q(RD2_o), .clk(in_1), .clr(in_2));  // open: en
  Register #(.width(5)) register_3 (.D(multiplexer_3_out), .Q(rs_o), .clk(in_1), .clr(in_2));  // open: en
  Register #(.width(5)) register_4 (.D(multiplexer_4_out), .Q(rt_o), .clk(in_1), .clr(in_2));  // open: en
  Register #(.width(5)) register_5 (.D(multiplexer_5_out), .Q(rd_o), .clk(in_1), .clr(in_2));  // open: en
  Register #(.width(32)) register_6 (.D(multiplexer_6_out), .Q(out_22), .clk(in_1), .clr(in_2));  // open: en
  Register #(.width(32)) register_7 (.D(multiplexer_7_out), .Q(out_23), .clk(in_1), .clr(in_2));  // open: en
  Multiplexer #(.width(32), .enable("false")) multiplexer_8 (
    .in0(pc_i), .in1({32{1'b0}}), .out(multiplexer_8_out), .sel(in_13));
  Multiplexer #(.width(32), .enable("false")) multiplexer_9 (
    .in0(pc_4_i), .in1({32{1'b0}}), .out(multiplexer_9_out), .sel(in_13));
  Multiplexer #(.width(32), .enable("false")) multiplexer_10 (
    .in0(pc_8_i), .in1({32{1'b0}}), .out(multiplexer_10_out), .sel(in_13));
  Register #(.width(32)) register_8 (.D(multiplexer_8_out), .Q(pc_o), .clk(in_1), .clr(in_2));  // open: en
  Register #(.width(32)) register_9 (.D(multiplexer_9_out), .Q(pc_4_o), .clk(in_1), .clr(in_2));  // open: en
  Register #(.width(32)) register_10 (.D(multiplexer_10_out), .Q(pc_8_o), .clk(in_1), .clr(in_2));  // open: en

  // Other names for the same wires on the sheet: clk = in_1; clk_prime = in_1; flush = in_13; Reset = in_2
endmodule

module ALU (
  input  [31:0] A,
  input  [31:0] B,
  input  [3:0] ALUOp,
  output [31:0] out_4
);

  wire [31:0] adder_1_out, and_1_out, or_1_out, subtractor_1_out;

  assign and_1_out = B & A;  // AND_Gate and_1, 32 bits wide
  assign or_1_out = B | A;  // OR_Gate or_1, 32 bits wide
  Adder #(.width(32)) adder_1 (.a(A), .b(B), .out(adder_1_out));  // open: cin, cout
  Subtractor #(.width(32)) subtractor_1 (.a(A), .b(B), .out(subtractor_1_out));  // open: bin, bout
  Multiplexer #(.select(4), .width(32), .enable("false")) multiplexer_1 (
    .in0(and_1_out), .in1(or_1_out), .in2(adder_1_out), .in4(subtractor_1_out), .out(out_4), .sel(ALUOp));  // open: in3, in5, in6, in7, in8, in9, in10, in11, in12, in13, in14, in15
endmodule

module Reg_EM (
  input  in_1,
  input  in_2,
  input  [31:0] aluresult_i,
  input  [31:0] writedata_i,
  input  [4:0] writereg_i,
  input  [31:0] pc_i,
  input  [31:0] pc_4_i,
  input  [31:0] pc_8_i,
  input  [31:0] instr_i,
  output [31:0] out_10,
  output [31:0] out_11,
  output [4:0] out_12,
  output [31:0] pc_o,
  output [31:0] pc_4_o,
  output [31:0] pc_8_o,
  output [31:0] out_16
);

  Register #(.width(32)) register_1 (.D(aluresult_i), .Q(out_10), .clk(in_1), .clr(in_2));  // open: en
  Register #(.width(32)) register_2 (.D(pc_i), .Q(pc_o), .clk(in_1), .clr(in_2));  // open: en
  Register #(.width(32)) register_3 (.D(writedata_i), .Q(out_11), .clk(in_1), .clr(in_2));  // open: en
  Register #(.width(5)) register_4 (.D(writereg_i), .Q(out_12), .clk(in_1), .clr(in_2));  // open: en
  Register #(.width(32)) register_5 (.D(pc_4_i), .Q(pc_4_o), .clk(in_1), .clr(in_2));  // open: en
  Register #(.width(32)) register_6 (.D(pc_8_i), .Q(pc_8_o), .clk(in_1), .clr(in_2));  // open: en
  Register #(.width(32)) register_7 (.D(instr_i), .Q(out_16), .clk(in_1), .clr(in_2));  // open: en

  // Other names for the same wires on the sheet: clk = in_1; clk_prime = in_1; Reset = in_2
endmodule

module REG_MW (
  input  in_1,
  input  in_2,
  input  [4:0] writereg_i,
  input  [31:0] aluresult_i,
  input  [31:0] writedata_i,
  input  [31:0] readdata_i,
  input  [31:0] pc_i,
  input  [31:0] pc_4_i,
  input  [31:0] pc_8_i,
  input  [31:0] instr_i,
  input  [31:0] memaddr,
  input  [31:0] memdata,
  input  memwrite,
  output [4:0] out_14,
  output [31:0] out_15,
  output [31:0] out_16,
  output [31:0] out_17,
  output [31:0] pc_o,
  output [31:0] pc_4_o,
  output [31:0] pc_8_o,
  output [31:0] out_21,
  output [31:0] out_22,
  output [31:0] out_23,
  output out_24
);

  Register #(.width(5)) register_1 (.D(writereg_i), .Q(out_14), .clk(in_1), .clr(in_2));  // open: en
  Register #(.width(32)) register_2 (.D(aluresult_i), .Q(out_15), .clk(in_1), .clr(in_2));  // open: en
  Register #(.width(32)) register_3 (.D(writedata_i), .Q(out_16), .clk(in_1), .clr(in_2));  // open: en
  Register #(.width(32)) register_4 (.D(readdata_i), .Q(out_17), .clk(in_1), .clr(in_2));  // open: en
  Register #(.width(32)) register_5 (.D(pc_i), .Q(pc_o), .clk(in_1), .clr(in_2));  // open: en
  Register #(.width(32)) register_6 (.D(pc_4_i), .Q(pc_4_o), .clk(in_1), .clr(in_2));  // open: en
  Register #(.width(32)) register_7 (.D(pc_8_i), .Q(pc_8_o), .clk(in_1), .clr(in_2));  // open: en
  Register #(.width(32)) register_8 (.D(instr_i), .Q(out_21), .clk(in_1), .clr(in_2));  // open: en
  Register #(.width(32)) register_9 (.D(memaddr), .Q(out_22), .clk(in_1), .clr(in_2));  // open: en
  Register #(.width(32)) register_10 (.D(memdata), .Q(out_23), .clk(in_1), .clr(in_2));  // open: en
  Register #(.width(1)) register_11 (.D(memwrite), .Q(out_24), .clk(in_1), .clr(in_2));  // open: en

  // Other names for the same wires on the sheet: clk = in_1; clk_prime = in_1; Reset = in_2
endmodule

module forwardUnit (
  input  [4:0] s1_D,
  input  [4:0] s2_D,
  input  [4:0] s1_E,
  input  [4:0] s2_E,
  input  [4:0] des_E,
  input  [3:0] tNew_E,
  input  [4:0] s2_M,
  input  [3:0] tNew_M,
  input  [4:0] des_M,
  input  [3:0] tNew_W,
  input  [4:0] des_W,
  output [1:0] fRsDsel,
  output [1:0] fRtDsel,
  output [1:0] fRsEsel,
  output [1:0] fRtEsel,
  output fRtMsel
);

  wire and_1_out, and_2_out, and_3_out, and_4_out, and_5_out, and_6_out, and_7_out, and_8_out, and_9_out,
       comparator_1_eq, comparator_2_eq, comparator_3_eq, comparator_4_eq, comparator_5_eq, comparator_6_eq,
       comparator_7_eq, comparator_8_eq, comparator_9_eq, comparator_10_eq, comparator_11_eq,
       comparator_12_eq, comparator_13_eq, comparator_14_eq, comparator_15_eq, comparator_16_eq,
       comparator_17_eq, comparator_18_eq, comparator_19_eq, comparator_20_eq, comparator_21_eq,
       comparator_22_eq, comparator_23_eq, comparator_24_eq, comparator_25_eq, comparator_26_eq,
       comparator_27_eq, not_1_out, not_2_out, not_3_out, not_4_out, not_5_out, not_6_out, not_7_out,
       not_8_out, not_9_out;
  wire [1:0] multiplexer_1_out, multiplexer_2_out, multiplexer_5_out, multiplexer_6_out;

  not not_1 (not_1_out, comparator_1_eq);
  Comparator #(.width(5), .mode("unsigned")) comparator_1 (
    .a(s1_D), .b({5{1'b0}}), .eq(comparator_1_eq));  // open: gt, lt
  Comparator #(.width(5), .mode("unsigned")) comparator_2 (.a(s1_D), .b(des_M), .eq(comparator_2_eq));  // open: gt, lt
  Comparator #(.width(4), .mode("unsigned")) comparator_3 (
    .a(tNew_M), .b(4'b0000), .eq(comparator_3_eq));  // open: gt, lt
  Comparator #(.width(5), .mode("unsigned")) comparator_4 (
    .a(s1_D), .b({5{1'b0}}), .eq(comparator_4_eq));  // open: gt, lt
  not not_2 (not_2_out, comparator_4_eq);
  Comparator #(.width(5), .mode("unsigned")) comparator_5 (.a(s1_D), .b(des_E), .eq(comparator_5_eq));  // open: gt, lt
  Comparator #(.width(4), .mode("unsigned")) comparator_6 (
    .a(tNew_E), .b(4'b0000), .eq(comparator_6_eq));  // open: gt, lt
  Comparator #(.width(5), .mode("unsigned")) comparator_7 (
    .a(s2_D), .b({5{1'b0}}), .eq(comparator_7_eq));  // open: gt, lt
  Comparator #(.width(5), .mode("unsigned")) comparator_8 (.a(s2_D), .b(des_M), .eq(comparator_8_eq));  // open: gt, lt
  Comparator #(.width(4), .mode("unsigned")) comparator_9 (
    .a(tNew_M), .b(4'b0000), .eq(comparator_9_eq));  // open: gt, lt
  Comparator #(.width(5), .mode("unsigned")) comparator_10 (
    .a(s2_D), .b({5{1'b0}}), .eq(comparator_10_eq));  // open: gt, lt
  Comparator #(.width(5), .mode("unsigned")) comparator_11 (
    .a(s2_D), .b(des_E), .eq(comparator_11_eq));  // open: gt, lt
  Comparator #(.width(4), .mode("unsigned")) comparator_12 (
    .a(tNew_E), .b(4'b0000), .eq(comparator_12_eq));  // open: gt, lt
  and and_1 (and_1_out, not_1_out, comparator_2_eq, comparator_3_eq);
  and and_2 (and_2_out, not_2_out, comparator_5_eq, comparator_6_eq);
  not not_3 (not_3_out, comparator_7_eq);
  not not_4 (not_4_out, comparator_10_eq);
  Multiplexer #(.width(2)) multiplexer_1 (
    .in0(2'b00), .in1(2'b10), .out(multiplexer_1_out), .sel(and_1_out));  // open: en
  and and_3 (and_3_out, not_3_out, comparator_8_eq, comparator_9_eq);
  and and_4 (and_4_out, not_4_out, comparator_11_eq, comparator_12_eq);
  Multiplexer #(.width(2)) multiplexer_2 (
    .in0(2'b00), .in1(2'b10), .out(multiplexer_2_out), .sel(and_3_out));  // open: en
  Multiplexer #(.width(2)) multiplexer_3 (
    .in0(multiplexer_1_out), .in1(2'b01), .out(fRsDsel), .sel(and_2_out));  // open: en
  Multiplexer #(.width(2)) multiplexer_4 (
    .in0(multiplexer_2_out), .in1(2'b01), .out(fRtDsel), .sel(and_4_out));  // open: en
  Comparator #(.width(5), .mode("unsigned")) comparator_13 (
    .a(s1_E), .b({5{1'b0}}), .eq(comparator_13_eq));  // open: gt, lt
  Comparator #(.width(5), .mode("unsigned")) comparator_14 (
    .a(s1_E), .b(des_W), .eq(comparator_14_eq));  // open: gt, lt
  Comparator #(.width(4), .mode("unsigned")) comparator_15 (
    .a(tNew_W), .b(4'b0000), .eq(comparator_15_eq));  // open: gt, lt
  Comparator #(.width(5), .mode("unsigned")) comparator_16 (
    .a(s1_E), .b({5{1'b0}}), .eq(comparator_16_eq));  // open: gt, lt
  Comparator #(.width(5), .mode("unsigned")) comparator_17 (
    .a(s1_E), .b(des_M), .eq(comparator_17_eq));  // open: gt, lt
  Comparator #(.width(4), .mode("unsigned")) comparator_18 (
    .a(tNew_M), .b(4'b0000), .eq(comparator_18_eq));  // open: gt, lt
  Comparator #(.width(5), .mode("unsigned")) comparator_19 (
    .a(s2_E), .b({5{1'b0}}), .eq(comparator_19_eq));  // open: gt, lt
  Comparator #(.width(5), .mode("unsigned")) comparator_20 (
    .a(s2_E), .b(des_W), .eq(comparator_20_eq));  // open: gt, lt
  Comparator #(.width(4), .mode("unsigned")) comparator_21 (
    .a(tNew_W), .b(4'b0000), .eq(comparator_21_eq));  // open: gt, lt
  Comparator #(.width(5), .mode("unsigned")) comparator_22 (
    .a(s2_E), .b({5{1'b0}}), .eq(comparator_22_eq));  // open: gt, lt
  Comparator #(.width(5), .mode("unsigned")) comparator_23 (
    .a(s2_E), .b(des_M), .eq(comparator_23_eq));  // open: gt, lt
  Comparator #(.width(4), .mode("unsigned")) comparator_24 (
    .a(tNew_M), .b(4'b0000), .eq(comparator_24_eq));  // open: gt, lt
  not not_5 (not_5_out, comparator_13_eq);
  not not_6 (not_6_out, comparator_16_eq);
  not not_7 (not_7_out, comparator_19_eq);
  not not_8 (not_8_out, comparator_22_eq);
  and and_5 (and_5_out, not_5_out, comparator_14_eq, comparator_15_eq);
  and and_6 (and_6_out, not_6_out, comparator_17_eq, comparator_18_eq);
  and and_7 (and_7_out, not_7_out, comparator_20_eq, comparator_21_eq);
  and and_8 (and_8_out, not_8_out, comparator_23_eq, comparator_24_eq);
  Multiplexer #(.width(2)) multiplexer_5 (
    .in0(2'b00), .in1(2'b10), .out(multiplexer_5_out), .sel(and_5_out));  // open: en
  Multiplexer #(.width(2)) multiplexer_6 (
    .in0(2'b00), .in1(2'b10), .out(multiplexer_6_out), .sel(and_7_out));  // open: en
  Multiplexer #(.width(2)) multiplexer_7 (
    .in0(multiplexer_5_out), .in1(2'b01), .out(fRsEsel), .sel(and_6_out));  // open: en
  Multiplexer #(.width(2)) multiplexer_8 (
    .in0(multiplexer_6_out), .in1(2'b01), .out(fRtEsel), .sel(and_8_out));  // open: en
  Comparator #(.width(5), .mode("unsigned")) comparator_25 (
    .a(s2_M), .b({5{1'b0}}), .eq(comparator_25_eq));  // open: gt, lt
  not not_9 (not_9_out, comparator_25_eq);
  Comparator #(.width(5), .mode("unsigned")) comparator_26 (
    .a(s2_M), .b(des_W), .eq(comparator_26_eq));  // open: gt, lt
  Comparator #(.width(4), .mode("unsigned")) comparator_27 (
    .a(tNew_W), .b(4'b0000), .eq(comparator_27_eq));  // open: gt, lt
  and and_9 (and_9_out, not_9_out, comparator_26_eq, comparator_27_eq);
  Multiplexer multiplexer_9 (.in0(1'b0), .in1(1'b1), .out(fRtMsel), .sel(and_9_out));  // open: en
endmodule

module Ctrl_E (
  input  [5:0] OP,
  input  [5:0] Func,
  output [1:0] Reg_Dst,
  output [3:0] ALUCtrl,
  output ALUSrc
);

  wire addiu_out, addu_out, beq_out, lb_out, lui_out, lw_out, ori_out, sb_out, subu_out, sw_out;

  and lw (lw_out, OP[5], ~OP[4], ~OP[3], ~OP[2], OP[1], OP[0]);  // AND_Gate
  and sw (sw_out, OP[5], ~OP[4], OP[3], ~OP[2], OP[1], OP[0]);  // AND_Gate
  and addu (addu_out, ~OP[5], ~OP[4], ~OP[3], ~OP[2], ~OP[1], ~OP[0], Func[5], ~Func[4], ~Func[3], ~Func[2], ~Func[1], Func[0]);  // AND_Gate
  and subu (subu_out, ~OP[5], ~OP[4], ~OP[3], ~OP[2], ~OP[1], ~OP[0], Func[5], ~Func[4], ~Func[3], ~Func[2], Func[1], Func[0]);  // AND_Gate
  and ori (ori_out, ~OP[5], ~OP[4], OP[3], OP[2], ~OP[1], OP[0]);  // AND_Gate
  and addiu (addiu_out, ~OP[5], ~OP[4], OP[3], ~OP[2], ~OP[1], OP[0]);  // AND_Gate
  and lui (lui_out, ~OP[5], ~OP[4], OP[3], OP[2], OP[1], OP[0]);  // AND_Gate
  and jal (Reg_Dst[1], ~OP[5], ~OP[4], ~OP[3], ~OP[2], OP[1], OP[0]);  // AND_Gate
  // AND_Gate j has open pins: in0=OP[5], in1=OP[4], in2=OP[3], in3=OP[2], in4=OP[1], in5=OP[0], out=open
  and beq (beq_out, ~OP[5], ~OP[4], ~OP[3], OP[2], ~OP[1], ~OP[0]);  // AND_Gate
  // AND_Gate jr has open pins: in0=OP[5], in1=OP[4], in2=OP[3], in3=OP[2], in4=OP[1], in5=OP[0], in6=Func[5], in7=Func[4], in8=Func[3], in9=Func[2], in10=Func[1], in11=Func[0], out=open
  // AND_Gate bgtz has open pins: in0=OP[5], in1=OP[4], in2=OP[3], in3=OP[2], in4=OP[1], in5=OP[0], out=open
  and lb (lb_out, OP[5], ~OP[4], ~OP[3], ~OP[2], ~OP[1], ~OP[0]);  // AND_Gate
  and sb (sb_out, OP[5], ~OP[4], OP[3], ~OP[2], ~OP[1], ~OP[0]);  // AND_Gate
  or or_1 (ALUSrc, addu_out, subu_out);
  or or_2 (ALUCtrl[2], subu_out, beq_out);
  or or_3 (ALUCtrl[1], lw_out, sw_out, addu_out, addiu_out, lb_out, sb_out);
  or or_4 (ALUCtrl[0], ori_out, lui_out);
  or or_5 (Reg_Dst[0], addu_out, subu_out);

  assign ALUCtrl[3] = 1'b0;
endmodule

module DM (
  input  lb,
  input  in_2,
  input  reset,
  input  sb,
  input  [31:0] in_5,
  input  [31:0] in_6,
  input  MemW,
  input  MemR,
  output [31:0] RD
);

  wire or_1_out, pull_resistor_1_node;
  wire [31:0] bit_extender_1_out, bit_extender_2_out, bit_extender_3_out, bit_extender_4_out, lb_data,
       multiplexer_1_out, out_word, sb_data;

  Multiplexer #(.width(32), .enable("false")) multiplexer_1 (
    .in0(in_6), .in1(sb_data), .out(multiplexer_1_out), .sel(sb));
  assign bit_extender_1_out = {{24{1'b0}}, out_word[7:0]};  // Bit_Extender bit_extender_1
  assign bit_extender_2_out = {{24{1'b0}}, out_word[15:8]};  // Bit_Extender bit_extender_2
  assign bit_extender_3_out = {{24{1'b0}}, out_word[23:16]};  // Bit_Extender bit_extender_3
  assign bit_extender_4_out = {{24{1'b0}}, out_word[31:24]};  // Bit_Extender bit_extender_4
  or or_1 (or_1_out, MemR, pull_resistor_1_node);
  Pull_Resistor #(.pull(1)) pull_resistor_1 (.node(pull_resistor_1_node));
  RAM #(.addrWidth(5), .dataWidth(32), .bus("separate")) ram_1 (
    .addr(in_5[6:2]), .din(multiplexer_1_out), .data(out_word), .str(MemW), .clk(in_2), .ld(or_1_out),
    .clr(reset));  // open: sel
  Multiplexer #(.select(2), .width(32), .enable("false")) multiplexer_2 (
    .in0(bit_extender_1_out), .in1(bit_extender_2_out), .in2(bit_extender_3_out), .in3(bit_extender_4_out),
    .out(lb_data), .sel(in_5[1:0]));
  Multiplexer #(.select(2), .width(32), .enable("false")) multiplexer_3 (
    .in0({out_word[31:8], in_6[7:0]}), .in1({out_word[31:16], in_6[7:0], out_word[7:0]}),
    .in2({out_word[31:24], in_6[7:0], out_word[15:0]}), .in3({in_6[7:0], out_word[23:0]}), .out(sb_data),
    .sel(in_5[1:0]));
  Multiplexer #(.width(32), .enable("false")) multiplexer_4 (.in0(out_word), .in1(lb_data), .out(RD), .sel(lb));

  // Other names for the same wires on the sheet: in_word[31:0] = in_6; Clk_prime = in_2; Offs[1:0] = in_5[1:0]
endmodule

module Ctrl_M (
  input  [5:0] OP,
  input  [5:0] Func,
  output WM,
  output RM,
  output lb,
  output sb
);

  wire sw_out;

  and lw (RM, OP[5], ~OP[4], ~OP[3], ~OP[2], OP[1], OP[0]);  // AND_Gate
  and sw (sw_out, OP[5], ~OP[4], OP[3], ~OP[2], OP[1], OP[0]);  // AND_Gate
  // AND_Gate addu has open pins: in0=OP[5], in1=OP[4], in2=OP[3], in3=OP[2], in4=OP[1], in5=OP[0], in6=Func[5], in7=Func[4], in8=Func[3], in9=Func[2], in10=Func[1], in11=Func[0], out=open
  // AND_Gate subu has open pins: in0=OP[5], in1=OP[4], in2=OP[3], in3=OP[2], in4=OP[1], in5=OP[0], in6=Func[5], in7=Func[4], in8=Func[3], in9=Func[2], in10=Func[1], in11=Func[0], out=open
  // AND_Gate ori has open pins: in0=OP[5], in1=OP[4], in2=OP[3], in3=OP[2], in4=OP[1], in5=OP[0], out=open
  // AND_Gate addui has open pins: in0=OP[5], in1=OP[4], in2=OP[3], in3=OP[2], in4=OP[1], in5=OP[0], out=open
  // AND_Gate lui has open pins: in0=OP[5], in1=OP[4], in2=OP[3], in3=OP[2], in4=OP[1], in5=OP[0], out=open
  // AND_Gate jal has open pins: in0=OP[5], in1=OP[4], in2=OP[3], in3=OP[2], in4=OP[1], in5=OP[0], out=open
  // AND_Gate j has open pins: in0=OP[5], in1=OP[4], in2=OP[3], in3=OP[2], in4=OP[1], in5=OP[0], out=open
  // AND_Gate beq has open pins: in0=OP[5], in1=OP[4], in2=OP[3], in3=OP[2], in4=OP[1], in5=OP[0], out=open
  // AND_Gate jr has open pins: in0=OP[5], in1=OP[4], in2=OP[3], in3=OP[2], in4=OP[1], in5=OP[0], in6=Func[5], in7=Func[4], in8=Func[3], in9=Func[2], in10=Func[1], in11=Func[0], out=open
  // AND_Gate bgtz has open pins: in0=OP[5], in1=OP[4], in2=OP[3], in3=OP[2], in4=OP[1], in5=OP[0], out=open
  and u_lb (lb, OP[5], ~OP[4], ~OP[3], ~OP[2], ~OP[1], ~OP[0]);  // AND_Gate
  and u_sb (sb, OP[5], ~OP[4], OP[3], ~OP[2], ~OP[1], ~OP[0]);  // AND_Gate
  or or_1 (WM, sw_out, sb);
endmodule

module Ctrl_W (
  input  [5:0] OP,
  input  [5:0] Func,
  output WriteReg,
  output [1:0] WD_Op
);

  wire addu_out, addui_out, jal_out, lb_out, lui_out, lw_out, ori_out, subu_out;

  and lw (lw_out, OP[5], ~OP[4], ~OP[3], ~OP[2], OP[1], OP[0]);  // AND_Gate
  // AND_Gate sw has open pins: in0=OP[5], in1=OP[4], in2=OP[3], in3=OP[2], in4=OP[1], in5=OP[0], out=open
  and addu (addu_out, ~OP[5], ~OP[4], ~OP[3], ~OP[2], ~OP[1], ~OP[0], Func[5], ~Func[4], ~Func[3], ~Func[2], ~Func[1], Func[0]);  // AND_Gate
  and subu (subu_out, ~OP[5], ~OP[4], ~OP[3], ~OP[2], ~OP[1], ~OP[0], Func[5], ~Func[4], ~Func[3], ~Func[2], Func[1], Func[0]);  // AND_Gate
  and ori (ori_out, ~OP[5], ~OP[4], OP[3], OP[2], ~OP[1], OP[0]);  // AND_Gate
  and addui (addui_out, ~OP[5], ~OP[4], OP[3], ~OP[2], ~OP[1], OP[0]);  // AND_Gate
  and lui (lui_out, ~OP[5], ~OP[4], OP[3], OP[2], OP[1], OP[0]);  // AND_Gate
  and jal (jal_out, ~OP[5], ~OP[4], ~OP[3], ~OP[2], OP[1], OP[0]);  // AND_Gate
  // AND_Gate j has open pins: in0=OP[5], in1=OP[4], in2=OP[3], in3=OP[2], in4=OP[1], in5=OP[0], out=open
  // AND_Gate beq has open pins: in0=OP[5], in1=OP[4], in2=OP[3], in3=OP[2], in4=OP[1], in5=OP[0], out=open
  // AND_Gate jr has open pins: in0=OP[5], in1=OP[4], in2=OP[3], in3=OP[2], in4=OP[1], in5=OP[0], in6=Func[5], in7=Func[4], in8=Func[3], in9=Func[2], in10=Func[1], in11=Func[0], out=open
  // AND_Gate bgtz has open pins: in0=OP[5], in1=OP[4], in2=OP[3], in3=OP[2], in4=OP[1], in5=OP[0], out=open
  and lb (lb_out, OP[5], ~OP[4], ~OP[3], ~OP[2], ~OP[1], ~OP[0]);  // AND_Gate
  // AND_Gate sb has open pins: in0=OP[5], in1=OP[4], in2=OP[3], in3=OP[2], in4=OP[1], in5=OP[0], out=open
  or or_1 (WriteReg, lw_out, addu_out, subu_out, ori_out, addui_out, lui_out, jal_out, lb_out);
  or or_2 (WD_Op[1], lw_out, lb_out, jal_out);
  or or_3 (WD_Op[0], lb_out, addu_out, subu_out, ori_out, addui_out, lw_out, lui_out);
endmodule

module stallUnit (
  input  [4:0] s1_D,
  input  [4:0] s2_D,
  input  [1:0] tUse1_D,
  input  [1:0] tUse2_D,
  input  [4:0] des_E,
  input  [3:0] tNew_E,
  input  [3:0] tNew_M,
  input  [4:0] des_M,
  output Stall_F,
  output Stall_D,
  output flush_E
);

  wire and_1_out, and_2_out, and_3_out, and_4_out, comparator_1_eq, comparator_2_eq, comparator_3_lt,
       comparator_4_eq, comparator_5_eq, comparator_6_lt, comparator_7_eq, comparator_8_eq, comparator_9_lt,
       comparator_10_eq, comparator_11_eq, comparator_12_lt, not_1_out, not_2_out, not_3_out, not_4_out;
  wire [3:0] tUse1_D_t, tUse2_D_t;

  Comparator #(.width(5), .mode("unsigned")) comparator_1 (
    .a(s1_D), .b({5{1'b0}}), .eq(comparator_1_eq));  // open: gt, lt
  Comparator #(.width(5), .mode("unsigned")) comparator_2 (.a(s1_D), .b(des_E), .eq(comparator_2_eq));  // open: gt, lt
  Comparator #(.width(4), .mode("unsigned")) comparator_3 (
    .a(tUse1_D_t), .b(tNew_E), .lt(comparator_3_lt));  // open: gt, eq
  Comparator #(.width(5), .mode("unsigned")) comparator_4 (
    .a(s2_D), .b({5{1'b0}}), .eq(comparator_4_eq));  // open: gt, lt
  Comparator #(.width(5), .mode("unsigned")) comparator_5 (.a(s2_D), .b(des_E), .eq(comparator_5_eq));  // open: gt, lt
  Comparator #(.width(4), .mode("unsigned")) comparator_6 (
    .a(tUse2_D_t), .b(tNew_E), .lt(comparator_6_lt));  // open: gt, eq
  Comparator #(.width(5), .mode("unsigned")) comparator_7 (
    .a(s1_D), .b({5{1'b0}}), .eq(comparator_7_eq));  // open: gt, lt
  Comparator #(.width(5), .mode("unsigned")) comparator_8 (.a(s1_D), .b(des_M), .eq(comparator_8_eq));  // open: gt, lt
  Comparator #(.width(4), .mode("unsigned")) comparator_9 (
    .a(tUse1_D_t), .b(tNew_M), .lt(comparator_9_lt));  // open: gt, eq
  Comparator #(.width(5), .mode("unsigned")) comparator_10 (
    .a(s2_D), .b({5{1'b0}}), .eq(comparator_10_eq));  // open: gt, lt
  Comparator #(.width(5), .mode("unsigned")) comparator_11 (
    .a(s2_D), .b(des_M), .eq(comparator_11_eq));  // open: gt, lt
  Comparator #(.width(4), .mode("unsigned")) comparator_12 (
    .a(tUse2_D_t), .b(tNew_M), .lt(comparator_12_lt));  // open: gt, eq
  assign tUse1_D_t = {{2{1'b0}}, tUse1_D};  // Bit_Extender bit_extender_1
  not not_1 (not_1_out, comparator_1_eq);
  not not_2 (not_2_out, comparator_4_eq);
  not not_3 (not_3_out, comparator_7_eq);
  not not_4 (not_4_out, comparator_10_eq);
  and and_1 (and_1_out, not_1_out, comparator_2_eq, comparator_3_lt);
  and and_2 (and_2_out, not_2_out, comparator_5_eq, comparator_6_lt);
  and and_3 (and_3_out, not_3_out, comparator_8_eq, comparator_9_lt);
  and and_4 (and_4_out, not_4_out, comparator_11_eq, comparator_12_lt);
  assign tUse2_D_t = {{2{1'b0}}, tUse2_D};  // Bit_Extender bit_extender_2
  or or_1 (flush_E, and_1_out, and_2_out, and_3_out, and_4_out);

  assign Stall_D = flush_E;
  assign Stall_F = flush_E;

  // Other names for the same wires on the sheet: stall_flag = flush_E
endmodule

module SF_D (
  input  [31:0] Inst,
  output [1:0] tuse1_D,
  output [4:0] s1_D,
  output [1:0] tuse2_D,
  output [4:0] s2_D
);

  wire addu_out, addui_out, beq_out, bgtz_out, jr_out, lb_out, lw_out, ori_out, s1_D_t, s2_D_t, sb_out,
       subu_out, sw_out;
  wire [4:0] splitter_1_rs, splitter_1_rt;
  wire [5:0] Func, OP;

  splitter splitter_1 (
    .inst(Inst), .Op(OP), .Func(Func), .rs(splitter_1_rs), .rt(splitter_1_rt));  // open: rd, imm_16, add_26, shamt
  and lw (lw_out, OP[5], ~OP[4], ~OP[3], ~OP[2], OP[1], OP[0]);  // AND_Gate
  and sw (sw_out, OP[5], ~OP[4], OP[3], ~OP[2], OP[1], OP[0]);  // AND_Gate
  and addu (addu_out, ~OP[5], ~OP[4], ~OP[3], ~OP[2], ~OP[1], ~OP[0], Func[5], ~Func[4], ~Func[3], ~Func[2], ~Func[1], Func[0]);  // AND_Gate
  and subu (subu_out, ~OP[5], ~OP[4], ~OP[3], ~OP[2], ~OP[1], ~OP[0], Func[5], ~Func[4], ~Func[3], ~Func[2], Func[1], Func[0]);  // AND_Gate
  and ori (ori_out, ~OP[5], ~OP[4], OP[3], OP[2], ~OP[1], OP[0]);  // AND_Gate
  and addui (addui_out, ~OP[5], ~OP[4], OP[3], ~OP[2], ~OP[1], OP[0]);  // AND_Gate
  // AND_Gate lui has open pins: in0=OP[5], in1=OP[4], in2=OP[3], in3=OP[2], in4=OP[1], in5=OP[0], out=open
  // AND_Gate jal has open pins: in0=OP[5], in1=OP[4], in2=OP[3], in3=OP[2], in4=OP[1], in5=OP[0], out=open
  // AND_Gate j has open pins: in0=OP[5], in1=OP[4], in2=OP[3], in3=OP[2], in4=OP[1], in5=OP[0], out=open
  and beq (beq_out, ~OP[5], ~OP[4], ~OP[3], OP[2], ~OP[1], ~OP[0]);  // AND_Gate
  and jr (jr_out, ~OP[5], ~OP[4], ~OP[3], ~OP[2], ~OP[1], ~OP[0], ~Func[5], ~Func[4], Func[3], ~Func[2], ~Func[1], ~Func[0]);  // AND_Gate
  and bgtz (bgtz_out, ~OP[5], ~OP[4], ~OP[3], OP[2], OP[1], OP[0]);  // AND_Gate
  and lb (lb_out, OP[5], ~OP[4], ~OP[3], ~OP[2], ~OP[1], ~OP[0]);  // AND_Gate
  and sb (sb_out, OP[5], ~OP[4], OP[3], ~OP[2], ~OP[1], ~OP[0]);  // AND_Gate
  Multiplexer #(.width(5), .enable("false")) multiplexer_1 (
    .in0({5{1'b0}}), .in1(splitter_1_rs), .out(s1_D), .sel(s1_D_t));
  Multiplexer #(.width(5), .enable("false")) multiplexer_2 (
    .in0({5{1'b0}}), .in1(splitter_1_rt), .out(s2_D), .sel(s2_D_t));
  or or_1 (s1_D_t, lb_out, lw_out, sw_out, addu_out, subu_out, ori_out, addui_out, jr_out, beq_out, bgtz_out, sb_out);
  or or_2 (s2_D_t, sw_out, addu_out, subu_out, beq_out, sb_out);
  or or_3 (tuse1_D[0], lw_out, sw_out, addu_out, subu_out, ori_out, addui_out, lb_out, sb_out);
  or or_4 (tuse2_D[1], sw_out, sb_out);
  or or_5 (tuse2_D[0], addu_out, subu_out);

  assign tuse1_D[1] = 1'b0;
endmodule

module SF_E (
  input  [31:0] Inst,
  input  [31:0] ext_E,
  input  [31:0] pc_8,
  output [4:0] des_E,
  output [4:0] s1_E,
  output [4:0] s2_E,
  output [1:0] tuse1_E,
  output [1:0] tuse2_E,
  output [3:0] tnew_E,
  output [31:0] EtoD
);

  wire addu_out, addui_out, fwd_Op, lb_out, lui_out, lw_out, ori_out, s1_E_t, s2_E_t, sb_out, subu_out,
       sw_out;
  wire [1:0] des_E_t;
  wire [4:0] splitter_1_rd, splitter_1_rs, splitter_1_rt;
  wire [5:0] Func, OP;

  splitter splitter_1 (
    .inst(Inst), .Op(OP), .Func(Func), .rs(splitter_1_rs), .rt(splitter_1_rt), .rd(splitter_1_rd));  // open: imm_16, add_26, shamt
  and lw (lw_out, OP[5], ~OP[4], ~OP[3], ~OP[2], OP[1], OP[0]);  // AND_Gate
  and sw (sw_out, OP[5], ~OP[4], OP[3], ~OP[2], OP[1], OP[0]);  // AND_Gate
  and addu (addu_out, ~OP[5], ~OP[4], ~OP[3], ~OP[2], ~OP[1], ~OP[0], Func[5], ~Func[4], ~Func[3], ~Func[2], ~Func[1], Func[0]);  // AND_Gate
  and subu (subu_out, ~OP[5], ~OP[4], ~OP[3], ~OP[2], ~OP[1], ~OP[0], Func[5], ~Func[4], ~Func[3], ~Func[2], Func[1], Func[0]);  // AND_Gate
  and ori (ori_out, ~OP[5], ~OP[4], OP[3], OP[2], ~OP[1], OP[0]);  // AND_Gate
  and addui (addui_out, ~OP[5], ~OP[4], OP[3], ~OP[2], ~OP[1], OP[0]);  // AND_Gate
  and lui (lui_out, ~OP[5], ~OP[4], OP[3], OP[2], OP[1], OP[0]);  // AND_Gate
  and jal (fwd_Op, ~OP[5], ~OP[4], ~OP[3], ~OP[2], OP[1], OP[0]);  // AND_Gate
  // AND_Gate j has open pins: in0=OP[5], in1=OP[4], in2=OP[3], in3=OP[2], in4=OP[1], in5=OP[0], out=open
  // AND_Gate beq has open pins: in0=OP[5], in1=OP[4], in2=OP[3], in3=OP[2], in4=OP[1], in5=OP[0], out=open
  // AND_Gate jr has open pins: in0=OP[5], in1=OP[4], in2=OP[3], in3=OP[2], in4=OP[1], in5=OP[0], in6=Func[5], in7=Func[4], in8=Func[3], in9=Func[2], in10=Func[1], in11=Func[0], out=open
  and lb (lb_out, OP[5], ~OP[4], ~OP[3], ~OP[2], ~OP[1], ~OP[0]);  // AND_Gate
  and sb (sb_out, OP[5], ~OP[4], OP[3], ~OP[2], ~OP[1], ~OP[0]);  // AND_Gate
  or or_1 (s1_E_t, lw_out, sw_out, addu_out, subu_out, ori_out, addui_out, lb_out, sb_out);
  Multiplexer #(.select(2), .width(5), .enable("false")) multiplexer_1 (
    .in0({5{1'b0}}), .in1(splitter_1_rd), .in2(splitter_1_rt), .in3({5{1'b1}}), .out(des_E), .sel(des_E_t));
  Multiplexer #(.width(5), .enable("false")) multiplexer_2 (
    .in0({5{1'b0}}), .in1(splitter_1_rs), .out(s1_E), .sel(s1_E_t));
  Multiplexer #(.width(5), .enable("false")) multiplexer_3 (
    .in0({5{1'b0}}), .in1(splitter_1_rt), .out(s2_E), .sel(s2_E_t));
  Multiplexer #(.width(32), .enable("false")) multiplexer_4 (.in0(ext_E), .in1(pc_8), .out(EtoD), .sel(fwd_Op));
  or or_2 (s2_E_t, sw_out, addu_out, subu_out, sb_out);
  or or_3 (des_E_t[1], lw_out, ori_out, addui_out, lui_out, fwd_Op, lb_out);
  or or_4 (des_E_t[0], addu_out, subu_out, fwd_Op);
  buf or_5 (tuse2_E[1], 1'b0);  // OR_Gate
  or or_6 (tuse2_E[0], sw_out, sb_out);
  Pull_Resistor pull_resistor_1 (.node(tnew_E));
  or or_7 (tnew_E[1], lw_out, lb_out);
  or or_8 (tnew_E[0], addu_out, subu_out, ori_out, addui_out);

  assign tuse1_E = 2'b00;

  // Notes on the sheet:
  //   0:$0  1:rd  2:rt  3:$31
endmodule

module SF_M (
  input  [31:0] Inst,
  input  [31:0] ALUOut,
  input  [31:0] pc_8,
  output [4:0] des_M,
  output [4:0] s2_M,
  output [1:0] tuse2_M,
  output [3:0] tnew_M,
  output [31:0] MtoD
);

  wire addu_out, addui_out, lb_out, lui_out, lw_out, ori_out, s2_M_t, sb_out, subu_out, sw_out;
  wire [1:0] des_M_t, fwd_Op;
  wire [4:0] splitter_1_rd, splitter_1_rt;
  wire [5:0] Func, OP;
  wire [15:0] splitter_1_imm_16;
  wire [31:0] bit_extender_1_out, shifter_1_out;

  splitter splitter_1 (
    .inst(Inst), .Op(OP), .Func(Func), .rt(splitter_1_rt), .rd(splitter_1_rd), .imm_16(splitter_1_imm_16));  // open: rs, add_26, shamt
  and lw (lw_out, OP[5], ~OP[4], ~OP[3], ~OP[2], OP[1], OP[0]);  // AND_Gate
  and sw (sw_out, OP[5], ~OP[4], OP[3], ~OP[2], OP[1], OP[0]);  // AND_Gate
  and addu (addu_out, ~OP[5], ~OP[4], ~OP[3], ~OP[2], ~OP[1], ~OP[0], Func[5], ~Func[4], ~Func[3], ~Func[2], ~Func[1], Func[0]);  // AND_Gate
  and subu (subu_out, ~OP[5], ~OP[4], ~OP[3], ~OP[2], ~OP[1], ~OP[0], Func[5], ~Func[4], ~Func[3], ~Func[2], Func[1], Func[0]);  // AND_Gate
  and ori (ori_out, ~OP[5], ~OP[4], OP[3], OP[2], ~OP[1], OP[0]);  // AND_Gate
  and addui (addui_out, ~OP[5], ~OP[4], OP[3], ~OP[2], ~OP[1], OP[0]);  // AND_Gate
  and lui (lui_out, ~OP[5], ~OP[4], OP[3], OP[2], OP[1], OP[0]);  // AND_Gate
  and jal (fwd_Op[1], ~OP[5], ~OP[4], ~OP[3], ~OP[2], OP[1], OP[0]);  // AND_Gate
  // AND_Gate j has open pins: in0=OP[5], in1=OP[4], in2=OP[3], in3=OP[2], in4=OP[1], in5=OP[0], out=open
  // AND_Gate beq has open pins: in0=OP[5], in1=OP[4], in2=OP[3], in3=OP[2], in4=OP[1], in5=OP[0], out=open
  // AND_Gate jr has open pins: in0=OP[5], in1=OP[4], in2=OP[3], in3=OP[2], in4=OP[1], in5=OP[0], in6=Func[5], in7=Func[4], in8=Func[3], in9=Func[2], in10=Func[1], in11=Func[0], out=open
  and lb (lb_out, OP[5], ~OP[4], ~OP[3], ~OP[2], ~OP[1], ~OP[0]);  // AND_Gate
  and sb (sb_out, OP[5], ~OP[4], OP[3], ~OP[2], ~OP[1], ~OP[0]);  // AND_Gate
  assign bit_extender_1_out = {{16{1'b0}}, splitter_1_imm_16};  // Bit_Extender bit_extender_1
  Shifter #(.width(32)) shifter_1 (.in(bit_extender_1_out), .\dist (5'b10000), .out(shifter_1_out));
  Multiplexer #(.select(2), .width(5), .enable("false")) multiplexer_1 (
    .in0({5{1'b0}}), .in1(splitter_1_rd), .in2(splitter_1_rt), .in3({5{1'b1}}), .out(des_M), .sel(des_M_t));
  Multiplexer #(.width(5), .enable("false")) multiplexer_2 (
    .in0({5{1'b0}}), .in1(splitter_1_rt), .out(s2_M), .sel(s2_M_t));
  Multiplexer #(.select(2), .width(32), .enable("false")) multiplexer_3 (
    .in0(shifter_1_out), .in1(ALUOut), .in2(pc_8), .out(MtoD), .sel(fwd_Op));  // open: in3
  or or_1 (s2_M_t, sw_out, sb_out);
  or or_2 (des_M_t[1], lw_out, ori_out, addui_out, lui_out, fwd_Op[1], lb_out);
  or or_3 (des_M_t[0], addu_out, subu_out, fwd_Op[1]);
  Pull_Resistor pull_resistor_1 (.node(tnew_M));
  or or_4 (tnew_M[0], lw_out, lb_out);
  or or_5 (fwd_Op[0], addu_out, subu_out, ori_out, addui_out);

  assign tuse2_M = 2'b00;
  // also tied to GND on the sheet: tnew_M[1]

  // Notes on the sheet:
  //   0:ext  1:ALUOut  2:pc+8
  //   0:$0  1:rd  2:rt  3:$31
endmodule

module SF_W (
  input  [31:0] Inst,
  input  [31:0] aluresult,
  input  [31:0] pc_8,
  input  [31:0] readData,
  output [4:0] des_W,
  output [3:0] tnew_W,
  output [31:0] WtoD
);

  wire addu_out, addui_out, jal_out, lb_out, lui_out, lw_out, ori_out, subu_out;
  wire [1:0] des_W_t, fwd_Op;
  wire [4:0] splitter_1_rd, splitter_1_rt;
  wire [5:0] Func, OP;
  wire [15:0] splitter_1_imm_16;
  wire [31:0] bit_extender_1_out, shifter_1_out;

  splitter splitter_1 (
    .inst(Inst), .Op(OP), .Func(Func), .rt(splitter_1_rt), .rd(splitter_1_rd), .imm_16(splitter_1_imm_16));  // open: rs, add_26, shamt
  and lw (lw_out, OP[5], ~OP[4], ~OP[3], ~OP[2], OP[1], OP[0]);  // AND_Gate
  // AND_Gate sw has open pins: in0=OP[5], in1=OP[4], in2=OP[3], in3=OP[2], in4=OP[1], in5=OP[0], out=open
  and addu (addu_out, ~OP[5], ~OP[4], ~OP[3], ~OP[2], ~OP[1], ~OP[0], Func[5], ~Func[4], ~Func[3], ~Func[2], ~Func[1], Func[0]);  // AND_Gate
  and subu (subu_out, ~OP[5], ~OP[4], ~OP[3], ~OP[2], ~OP[1], ~OP[0], Func[5], ~Func[4], ~Func[3], ~Func[2], Func[1], Func[0]);  // AND_Gate
  and ori (ori_out, ~OP[5], ~OP[4], OP[3], OP[2], ~OP[1], OP[0]);  // AND_Gate
  and addui (addui_out, ~OP[5], ~OP[4], OP[3], ~OP[2], ~OP[1], OP[0]);  // AND_Gate
  and lui (lui_out, ~OP[5], ~OP[4], OP[3], OP[2], OP[1], OP[0]);  // AND_Gate
  and jal (jal_out, ~OP[5], ~OP[4], ~OP[3], ~OP[2], OP[1], OP[0]);  // AND_Gate
  // AND_Gate j has open pins: in0=OP[5], in1=OP[4], in2=OP[3], in3=OP[2], in4=OP[1], in5=OP[0], out=open
  // AND_Gate beq has open pins: in0=OP[5], in1=OP[4], in2=OP[3], in3=OP[2], in4=OP[1], in5=OP[0], out=open
  // AND_Gate jr has open pins: in0=OP[5], in1=OP[4], in2=OP[3], in3=OP[2], in4=OP[1], in5=OP[0], in6=Func[5], in7=Func[4], in8=Func[3], in9=Func[2], in10=Func[1], in11=Func[0], out=open
  and lb (lb_out, OP[5], ~OP[4], ~OP[3], ~OP[2], ~OP[1], ~OP[0]);  // AND_Gate
  // AND_Gate sb has open pins: in0=OP[5], in1=OP[4], in2=OP[3], in3=OP[2], in4=OP[1], in5=OP[0], out=open
  assign bit_extender_1_out = {{16{1'b0}}, splitter_1_imm_16};  // Bit_Extender bit_extender_1
  Shifter #(.width(32)) shifter_1 (.in(bit_extender_1_out), .\dist (5'b10000), .out(shifter_1_out));
  Multiplexer #(.select(2), .width(5), .enable("false")) multiplexer_1 (
    .in0({5{1'b0}}), .in1(splitter_1_rd), .in2(splitter_1_rt), .in3({5{1'b1}}), .out(des_W), .sel(des_W_t));
  Multiplexer #(.select(2), .width(32), .enable("false")) multiplexer_2 (
    .in0(shifter_1_out), .in1(aluresult), .in2(pc_8), .in3(readData), .out(WtoD), .sel(fwd_Op));
  or or_1 (des_W_t[1], lw_out, ori_out, addui_out, lui_out, jal_out, lb_out);
  or or_2 (des_W_t[0], addu_out, subu_out, jal_out);
  or or_3 (fwd_Op[1], lw_out, lb_out, jal_out);
  or or_4 (fwd_Op[0], addu_out, subu_out, ori_out, addui_out, lw_out, lb_out);

  assign tnew_W = 4'b0000;

  // Notes on the sheet:
  //   0:ext  1:ALUOut  2:pc+8  3:RD
  //   0:$0  1:rd  2:rt  3:$31
endmodule
