// Logisim project cpu -cache -流水线寄存器D-E.circ as structural Verilog: 1 circuit, main circuit D_E_reg
module D_E_reg (
  input  in_1,
  input  in_2,
  input  [31:0] pc_i,
  input  [31:0] RD1_i,
  input  [31:0] pc_4_i,
  input  [31:0] RD2_i,
  input  [31:0] pc_8_i,
  input  [4:0] rs_i,
  input  [4:0] rt_i,
  input  [4:0] rd_i,
  input  [31:0] instr_i,
  input  in_12,
  output [31:0] pc_o,
  output [31:0] RD1_o,
  output [31:0] pc_4_o,
  output [31:0] RD2_o,
  output [31:0] pc_8_o,
  output [4:0] rs_o,
  output [4:0] rt_o,
  output [4:0] rd_o,
  output [31:0] out_21
);

  wire [4:0] multiplexer_3_out, multiplexer_4_out, multiplexer_5_out;
  wire [31:0] multiplexer_1_out, multiplexer_2_out, multiplexer_6_out, multiplexer_7_out, multiplexer_8_out,
       multiplexer_9_out;

  Multiplexer #(.width(32), .enable("false")) multiplexer_1 (
    .in0(RD1_i), .in1({32{1'b0}}), .out(multiplexer_1_out), .sel(in_12));
  Multiplexer #(.width(32), .enable("false")) multiplexer_2 (
    .in0(RD2_i), .in1({32{1'b0}}), .out(multiplexer_2_out), .sel(in_12));
  Multiplexer #(.width(5), .enable("false")) multiplexer_3 (
    .in0(rs_i), .in1({5{1'b0}}), .out(multiplexer_3_out), .sel(in_12));
  Multiplexer #(.width(5), .enable("false")) multiplexer_4 (
    .in0(rt_i), .in1({5{1'b0}}), .out(multiplexer_4_out), .sel(in_12));
  Multiplexer #(.width(5), .enable("false")) multiplexer_5 (
    .in0(rd_i), .in1({5{1'b0}}), .out(multiplexer_5_out), .sel(in_12));
  Multiplexer #(.width(32), .enable("false")) multiplexer_6 (
    .in0(instr_i), .in1({32{1'b0}}), .out(multiplexer_6_out), .sel(in_12));
  Register #(.width(32)) register_1 (.D(multiplexer_1_out), .Q(RD1_o), .clk(in_1), .clr(in_2));  // open: en
  Register #(.width(32)) register_2 (.D(multiplexer_2_out), .Q(RD2_o), .clk(in_1), .clr(in_2));  // open: en
  Register #(.width(5)) register_3 (.D(multiplexer_3_out), .Q(rs_o), .clk(in_1), .clr(in_2));  // open: en
  Register #(.width(5)) register_4 (.D(multiplexer_4_out), .Q(rt_o), .clk(in_1), .clr(in_2));  // open: en
  Register #(.width(5)) register_5 (.D(multiplexer_5_out), .Q(rd_o), .clk(in_1), .clr(in_2));  // open: en
  Register #(.width(32)) register_6 (.D(multiplexer_6_out), .Q(out_21), .clk(in_1), .clr(in_2));  // open: en
  Multiplexer #(.width(32), .enable("false")) multiplexer_7 (
    .in0(pc_i), .in1({32{1'b0}}), .out(multiplexer_7_out), .sel(in_12));
  Multiplexer #(.width(32), .enable("false")) multiplexer_8 (
    .in0(pc_4_i), .in1({32{1'b0}}), .out(multiplexer_8_out), .sel(in_12));
  Multiplexer #(.width(32), .enable("false")) multiplexer_9 (
    .in0(pc_8_i), .in1({32{1'b0}}), .out(multiplexer_9_out), .sel(in_12));
  Register #(.width(32)) register_7 (.D(multiplexer_7_out), .Q(pc_o), .clk(in_1), .clr(in_2));  // open: en
  Register #(.width(32)) register_8 (.D(multiplexer_8_out), .Q(pc_4_o), .clk(in_1), .clr(in_2));  // open: en
  Register #(.width(32)) register_9 (.D(multiplexer_9_out), .Q(pc_8_o), .clk(in_1), .clr(in_2));  // open: en

  // Other names for the same wires on the sheet: clk = in_1; clk_prime = in_1; flush = in_12; Reset = in_2
endmodule
