// Logisim project cpu -cache -流水线寄存器E-M.circ as structural Verilog: 1 circuit, main circuit E_M_reg
module E_M_reg (
  input  in_1,
  input  in_2,
  input  [31:0] aluresult_i,
  input  [31:0] writedata_i,
  input  [4:0] writereg_i,
  input  [31:0] pc_i,
  input  [31:0] pc_4_i,
  input  [31:0] pc_8_i,
  input  [31:0] instr_i,
  output [31:0] out_10,
  output [31:0] out_11,
  output [4:0] out_12,
  output [31:0] pc_o,
  output [31:0] pc_4_o,
  output [31:0] pc_8_o,
  output [31:0] out_16
);

  Register #(.width(32)) register_1 (.D(aluresult_i), .Q(out_10), .clk(in_1), .clr(in_2));  // open: en
  Register #(.width(32)) register_2 (.D(writedata_i), .Q(out_11), .clk(in_1), .clr(in_2));  // open: en
  Register #(.width(5)) register_3 (.D(writereg_i), .Q(out_12), .clk(in_1), .clr(in_2));  // open: en
  Register #(.width(32)) register_4 (.D(pc_i), .Q(pc_o), .clk(in_1), .clr(in_2));  // open: en
  Register #(.width(32)) register_5 (.D(pc_4_i), .Q(pc_4_o), .clk(in_1), .clr(in_2));  // open: en
  Register #(.width(32)) register_6 (.D(pc_8_i), .Q(pc_8_o), .clk(in_1), .clr(in_2));  // open: en
  Register #(.width(32)) register_7 (.D(instr_i), .Q(out_16), .clk(in_1), .clr(in_2));  // open: en

  // Other names for the same wires on the sheet: clk = in_1; clk_prime = in_1; Reset = in_2
endmodule
