// Logisim project CPU.circ as structural Verilog: 14 circuits, main circuit main
module main (
  input  in_1,
  output [31:0] out_2,
  output out_3,
  output [4:0] out_4,
  output [31:0] out_5,
  output out_6,
  output [15:0] out_7,
  output [31:0] out_8
);

  wire CLK, control_1_alu_src, MemRead, Stop, zero;
  wire [1:0] control_1_ext_op, control_1_npc_op, control_1_reg_dst, control_1_reg_src;
  wire [3:0] control_1_alu_op;
  wire [4:0] addtorom_1_output_5, decoder_1_rd, decoder_1_rs, decoder_1_rt;
  wire [5:0] decoder_1_func, decoder_1_op;
  wire [15:0] decoder_1_imm16;
  wire [25:0] decoder_1__26add;
  wire [31:0] cache_1_outdata, ext_1_output_32, grf_1_rd1, MemAddr, multiplexer_3_out, npc_1_pc, pc_1_output;

  // Probe on control_1_npc_op
  NPC npc_1 (
    .PC(npc_1_pc), .imm_26(decoder_1__26add), .NPC(pc_1_output), .NPC_Op(control_1_npc_op), .zero(zero));  // open: PC_4, rs
  PC pc_1 (.Input(npc_1_pc), .Output(pc_1_output), .Reset(in_1), .CLK(CLK), .in_3(Stop));
  Clock clock_1 (.out(CLK));
  ADDtoROM addtorom_1 (.Input_32(pc_1_output), .Output_5(addtorom_1_output_5));
  // Probe on addtorom_1_output_5
  // Probe on pc_1_output
  // Probe on decoder_1__26add
  ROM #(.addrWidth(5), .dataWidth(32)) rom_1 (.addr(addtorom_1_output_5), .data(out_2));  // open: sel
  Decoder decoder_1 (
    .in_1(out_2), ._26Add(decoder_1__26add), .Op(decoder_1_op), .rs(decoder_1_rs), .rt(decoder_1_rt),
    .rd(decoder_1_rd), .imm16(decoder_1_imm16), .Func(decoder_1_func));  // open: Shamt
  // Probe on decoder_1_imm16
  Control control_1 (
    .OP(decoder_1_op), .Func(decoder_1_func), .ALU_Op(control_1_alu_op), .EXT_Op(control_1_ext_op),
    .ALU_Src(control_1_alu_src), .Mem_Wr(out_6), .Reg_Wr(out_3), .Reg_Src(control_1_reg_src),
    .NPC_Op(control_1_npc_op), .Reg_Dst(control_1_reg_dst), .MemRead(MemRead));
  EXT ext_1 (.Input_16(decoder_1_imm16), .EXT_Op(control_1_ext_op), .Output_32(ext_1_output_32));
  // Probe on control_1_reg_dst
  Multiplexer #(.select(2), .width(5), .enable("false")) multiplexer_1 (
    .in0(decoder_1_rd), .in1(decoder_1_rt), .out(out_4), .sel(control_1_reg_dst));  // open: in2, in3
  // Probe on control_1_alu_op
  // Probe on control_1_reg_src
  Multiplexer #(.select(2), .width(32), .enable("false")) multiplexer_2 (
    .in0({MemAddr[31:18], out_7, MemAddr[1:0]}), .in1(cache_1_outdata), .out(out_5), .sel(control_1_reg_src));  // open: in2, in3
  GRF grf_1 (
    .A1(decoder_1_rs), .A2(decoder_1_rt), .A3(out_4), .WD(out_5), .RD1(grf_1_rd1), .RD2(out_8), .clk(CLK),
    .reset(in_1), .we(out_3));
  Multiplexer #(.width(32), .enable("false")) multiplexer_3 (
    .in0(out_8), .in1(ext_1_output_32), .out(multiplexer_3_out), .sel(control_1_alu_src));
  // Probe on grf_1_rd1
  ALU alu_1 (
    .A(grf_1_rd1), .B(multiplexer_3_out), .ALUOp(control_1_alu_op), .zero(zero),
    .out_5({MemAddr[31:18], out_7, MemAddr[1:0]}));
  // Probe on {MemAddr[31:18], out_7, MemAddr[1:0]}
  // Probe on multiplexer_3_out
  Cache cache_1 (
    .MemAdd({MemAddr[31:18], out_7, MemAddr[1:0]}), .Indata(out_8), .OutData(cache_1_outdata), .Stop(Stop),
    .Str(out_6), .Clk(CLK), .Ld(MemRead), .Clr(in_1));  // open: All, Hit

  // Other names for the same wires on the sheet: Instr[31:0] = out_2; MemAddr[17:2] = out_7; MemData[31:0] = out_8;
  //   MemWrite = out_6; RegAddr[4:0] = out_4; RegData[31:0] = out_5; RegWrite = out_3; reset = in_1

  // Notes on the sheet:
  //   contents of rom_1 (hex, n*v repeats v):
  //   34211234 34025678 3403abcd ac010004 ac020008 8c040004
endmodule

// RF
module GRF (
  input  [4:0] A1,
  input  clk,
  input  reset,
  input  we,
  input  [4:0] A2,
  input  [4:0] A3,
  input  [31:0] WD,
  output [31:0] RD1,
  output [31:0] RD2
);

  wire [31:0] I0, I1, I2, I3, I4, I5, I6, I7, I8, I9, I10, I11, I12, I13, I14, I15, I16, I17, I18, I19, I20,
       I21, I22, I23, I24, I25, I26, I27, I28, I29, I30, I31, O0, O1, O2, O3, O4, O5, O6, O7, O8, O9, O10,
       O11, O12, O13, O14, O15, O16, O17, O18, O19, O20, O21, O22, O23, O24, O25, O26, O27, O28, O29, O30,
       O31;

  Demultiplexer #(.select(5), .width(32), .tristate("true")) demultiplexer_1 (
    .out0(I0), .out1(I1), .out2(I2), .out3(I3), .out4(I4), .out5(I5), .out6(I6), .out7(I7), .out8(I8),
    .out9(I9), .out10(I10), .out11(I11), .out12(I12), .out13(I13), .out14(I14), .out15(I15), .out16(I16),
    .out17(I17), .out18(I18), .out19(I19), .out20(I20), .out21(I21), .out22(I22), .out23(I23), .out24(I24),
    .out25(I25), .out26(I26), .out27(I27), .out28(I28), .out29(I29), .out30(I30), .out31(I31), .in(WD),
    .sel(A3));  // open: en
  Multiplexer #(.select(5), .width(32)) multiplexer_1 (
    .in0(O0), .in1(O1), .in2(O2), .in3(O3), .in4(O4), .in5(O5), .in6(O6), .in7(O7), .in8(O8), .in9(O9),
    .in10(O10), .in11(O11), .in12(O12), .in13(O13), .in14(O14), .in15(O15), .in16(O16), .in17(O17),
    .in18(O18), .in19(O19), .in20(O20), .in21(O21), .in22(O22), .in23(O23), .in24(O24), .in25(O25),
    .in26(O26), .in27(O27), .in28(O28), .in29(O29), .in30(O30), .in31(O31), .out(RD2), .sel(A2));  // open: en
  Multiplexer #(.select(5), .width(32)) multiplexer_2 (
    .in0(O0), .in1(O1), .in2(O2), .in3(O3), .in4(O4), .in5(O5), .in6(O6), .in7(O7), .in8(O8), .in9(O9),
    .in10(O10), .in11(O11), .in12(O12), .in13(O13), .in14(O14), .in15(O15), .in16(O16), .in17(O17),
    .in18(O18), .in19(O19), .in20(O20), .in21(O21), .in22(O22), .in23(O23), .in24(O24), .in25(O25),
    .in26(O26), .in27(O27), .in28(O28), .in29(O29), .in30(O30), .in31(O31), .out(RD1), .sel(A1));  // open: en
  Register #(.width(32)) register_1 (.D({32{1'b0}}), .en(we), .Q(O0), .clk(clk), .clr(reset));
  Register #(.width(32)) register_2 (.D(I8), .en(we), .Q(O8), .clk(clk), .clr(reset));
  Register #(.width(32)) register_3 (.D(I16), .en(we), .Q(O16), .clk(clk), .clr(reset));
  Register #(.width(32)) register_4 (.D(I24), .en(we), .Q(O24), .clk(clk), .clr(reset));
  Register #(.width(32)) register_5 (.D(I1), .en(we), .Q(O1), .clk(clk), .clr(reset));
  Register #(.width(32)) register_6 (.D(I9), .en(we), .Q(O9), .clk(clk), .clr(reset));
  Register #(.width(32)) register_7 (.D(I17), .en(we), .Q(O17), .clk(clk), .clr(reset));
  Register #(.width(32)) register_8 (.D(I25), .en(we), .Q(O25), .clk(clk), .clr(reset));
  Register #(.width(32)) register_9 (.D(I2), .en(we), .Q(O2), .clk(clk), .clr(reset));
  Register #(.width(32)) register_10 (.D(I10), .en(we), .Q(O10), .clk(clk), .clr(reset));
  Register #(.width(32)) register_11 (.D(I18), .en(we), .Q(O18), .clk(clk), .clr(reset));
  Register #(.width(32)) register_12 (.D(I26), .en(we), .Q(O26), .clk(clk), .clr(reset));
  Register #(.width(32)) register_13 (.D(I3), .en(we), .Q(O3), .clk(clk), .clr(reset));
  Register #(.width(32)) register_14 (.D(I11), .en(we), .Q(O11), .clk(clk), .clr(reset));
  Register #(.width(32)) register_15 (.D(I19), .en(we), .Q(O19), .clk(clk), .clr(reset));
  Register #(.width(32)) register_16 (.D(I27), .en(we), .Q(O27), .clk(clk), .clr(reset));
  Register #(.width(32)) register_17 (.D(I4), .en(we), .Q(O4), .clk(clk), .clr(reset));
  Register #(.width(32)) register_18 (.D(I12), .en(we), .Q(O12), .clk(clk), .clr(reset));
  Register #(.width(32)) register_19 (.D(I20), .en(we), .Q(O20), .clk(clk), .clr(reset));
  Register #(.width(32)) register_20 (.D(I28), .en(we), .Q(O28), .clk(clk), .clr(reset));
  Register #(.width(32)) register_21 (.D(I5), .en(we), .Q(O5), .clk(clk), .clr(reset));
  Register #(.width(32)) register_22 (.D(I13), .en(we), .Q(O13), .clk(clk), .clr(reset));
  Register #(.width(32)) register_23 (.D(I21), .en(we), .Q(O21), .clk(clk), .clr(reset));
  Register #(.width(32)) register_24 (.D(I29), .en(we), .Q(O29), .clk(clk), .clr(reset));
  Register #(.width(32)) register_25 (.D(I6), .en(we), .Q(O6), .clk(clk), .clr(reset));
  Register #(.width(32)) register_26 (.D(I14), .en(we), .Q(O14), .clk(clk), .clr(reset));
  Register #(.width(32)) register_27 (.D(I22), .en(we), .Q(O22), .clk(clk), .clr(reset));
  Register #(.width(32)) register_28 (.D(I30), .en(we), .Q(O30), .clk(clk), .clr(reset));
  Register #(.width(32)) register_29 (.D(I7), .en(we), .Q(O7), .clk(clk), .clr(reset));
  Register #(.width(32)) register_30 (.D(I15), .en(we), .Q(O15), .clk(clk), .clr(reset));
  Register #(.width(32)) register_31 (.D(I23), .en(we), .Q(O23), .clk(clk), .clr(reset));
  Register #(.width(32)) register_32 (.D(I31), .en(we), .Q(O31), .clk(clk), .clr(reset));
endmodule

module PC (
  input  [31:0] Input,
  input  Reset,
  input  in_3,
  input  CLK,
  output [31:0] Output
);

  wire not_1_out, or_1_out;
  wire [31:0] multiplexer_1_out;

  Multiplexer #(.width(32), .enable("false")) multiplexer_1 (
    .in0(Input), .in1(32'h3000), .out(multiplexer_1_out), .sel(Reset));
  or or_1 (or_1_out, Reset, not_1_out);
  not not_1 (not_1_out, in_3);
  Register #(.width(32)) register_1 (.D(multiplexer_1_out), .en(or_1_out), .Q(Output), .clk(CLK));  // open: clr
endmodule

module Control (
  input  [5:0] OP,
  input  [5:0] Func,
  output [1:0] NPC_Op,
  output [3:0] ALU_Op,
  output [1:0] EXT_Op,
  output ALU_Src,
  output Mem_Wr,
  output Reg_Wr,
  output [1:0] Reg_Src,
  output MemRead,
  output [1:0] Reg_Dst
);

  wire addu_out, subu_out;

  and lw (MemRead, OP[5], ~OP[4], ~OP[3], ~OP[2], OP[1], OP[0]);  // AND_Gate
  and sw (Mem_Wr, OP[5], ~OP[4], OP[3], ~OP[2], OP[1], OP[0]);  // AND_Gate
  and addu (addu_out, ~OP[5], ~OP[4], ~OP[3], ~OP[2], ~OP[1], ~OP[0], Func[5], ~Func[4], ~Func[3], ~Func[2], ~Func[1], Func[0]);  // AND_Gate
  and subu (subu_out, ~OP[5], ~OP[4], ~OP[3], ~OP[2], ~OP[1], ~OP[0], Func[5], ~Func[4], ~Func[3], ~Func[2], Func[1], Func[0]);  // AND_Gate
  and ori (ALU_Op[0], ~OP[5], ~OP[4], OP[3], OP[2], ~OP[1], OP[0]);  // AND_Gate
  and j (NPC_Op[1], ~OP[5], ~OP[4], ~OP[3], ~OP[2], OP[1], ~OP[0]);  // AND_Gate
  and beq (NPC_Op[0], ~OP[5], ~OP[4], ~OP[3], OP[2], ~OP[1], ~OP[0]);  // AND_Gate
  or or_1 (ALU_Op[1], MemRead, Mem_Wr, addu_out);
  or or_2 (ALU_Op[2], subu_out, NPC_Op[0]);
  or or_3 (ALU_Src, Mem_Wr, MemRead, ALU_Op[0]);
  or or_4 (Reg_Wr, MemRead, addu_out, subu_out, ALU_Op[0]);
  or or_5 (Reg_Dst[0], MemRead, ALU_Op[0]);

  assign ALU_Op[3] = 1'b0;
  assign EXT_Op = {1'b0, ALU_Op[0]};
  assign Reg_Dst[1] = 1'b0;
  assign Reg_Src = {1'b0, MemRead};
endmodule

module ALUcontrol (
  input  [1:0] ALUOp,
  input  [5:0] Func,
  output [3:0] ALUoperation
);

  wire [3:0] func_1_aluoperation;

  Func func_1 (.in_1(Func), .AlUoperation(func_1_aluoperation));
  Multiplexer #(.select(2), .width(4), .enable("false")) multiplexer_1 (
    .in0(4'b0010), .in1(4'b0001), .in2(func_1_aluoperation), .out(ALUoperation), .sel(ALUOp));  // open: in3
endmodule

module Func (
  input  [5:0] in_1,
  output [3:0] AlUoperation
);

  not not_1 (AlUoperation[1], in_1[2]);

  assign {AlUoperation[3:2], AlUoperation[0]} = {1'b0, in_1[1:0]};
endmodule

module Decoder (
  input  [31:0] in_1,
  output [25:0] _26Add,
  output [5:0] Op,
  output [4:0] rs,
  output [4:0] rt,
  output [4:0] rd,
  output [4:0] Shamt,
  output [15:0] imm16,
  output [5:0] Func
);


  assign _26Add = in_1[25:0];
  assign Func = in_1[5:0];
  assign imm16 = in_1[15:0];
  assign Op = in_1[31:26];
  assign rd = in_1[15:11];
  assign rs = in_1[25:21];
  assign rt = in_1[20:16];
  assign Shamt = in_1[10:6];
endmodule

module ALU (
  input  [31:0] A,
  input  [31:0] B,
  input  [3:0] ALUOp,
  output zero,
  output [31:0] out_5
);

  wire [31:0] adder_1_out, and_1_out, or_1_out, subtractor_1_out;

  assign and_1_out = B & A;  // AND_Gate and_1, 32 bits wide
  assign or_1_out = B | A;  // OR_Gate or_1, 32 bits wide
  Adder #(.width(32)) adder_1 (.a(A), .b(B), .out(adder_1_out));  // open: cin, cout
  Subtractor #(.width(32)) subtractor_1 (.a(A), .b(B), .out(subtractor_1_out));  // open: bin, bout
  Multiplexer #(.select(4), .width(32), .enable("false")) multiplexer_1 (
    .in0(and_1_out), .in1(or_1_out), .in2(adder_1_out), .in4(subtractor_1_out), .out(out_5), .sel(ALUOp));  // open: in3, in5, in6, in7, in8, in9, in10, in11, in12, in13, in14, in15
  Comparator #(.width(32)) comparator_1 (.a({32{1'b0}}), .b(out_5), .eq(zero));  // open: gt, lt
endmodule

// 32-5
module ADDtoROM (
  input  [31:0] Input_32,
  output [4:0] Output_5
);

  wire [31:0] subtractor_1_out;

  Subtractor #(.width(32)) subtractor_1 (
    .a(Input_32), .b(32'h3000), .out({subtractor_1_out[31:7], Output_5, subtractor_1_out[1:0]}));  // open: bin, bout
endmodule

// <<2
module _2_28 (
  input  [27:0] in_1,
  output [27:0] out_2
);

  Shifter #(.width(28)) shifter_1 (.in(in_1), .\dist (5'b00010), .out(out_2));
endmodule

// <<2
module _2_32 (
  input  [31:0] in_1,
  output [31:0] out_2
);

  Shifter #(.width(32)) shifter_1 (.in(in_1), .\dist (5'b00010), .out(out_2));
endmodule

module NPC (
  input  [1:0] NPC_Op,
  input  zero,
  input  [25:0] imm_26,
  input  [31:0] NPC,
  input  [31:0] rs,
  output [31:0] PC_4,
  output [31:0] PC
);

  wire [1:0] npc_op_1_op_2;
  wire [27:0] bit_extender_2_out, n2_28_1_out_2;
  wire [31:0] adder_2_out, bit_extender_1_out, n2_32_1_out_2;

  Adder #(.width(32)) adder_1 (.a(NPC), .b(32'h4), .out(PC_4));  // open: cin, cout
  _2_32 u_2_32_1 (.in_1(bit_extender_1_out), .out_2(n2_32_1_out_2));
  assign bit_extender_1_out = {{16{imm_26[15]}}, imm_26[15:0]};  // Bit_Extender bit_extender_1
  _2_28 u_2_28_1 (.in_1(bit_extender_2_out), .out_2(n2_28_1_out_2));
  assign bit_extender_2_out = {{2{imm_26[25]}}, imm_26};  // Bit_Extender bit_extender_2
  Adder #(.width(32)) adder_2 (.a(PC_4), .b(n2_32_1_out_2), .out(adder_2_out));  // open: cin, cout
  Multiplexer #(.select(2), .width(32), .enable("false")) multiplexer_1 (
    .in0(PC_4), .in1(adder_2_out), .in2({NPC[31:28], n2_28_1_out_2}), .in3(rs), .out(PC), .sel(npc_op_1_op_2));
  NPC_Op npc_op_1 (.Op(NPC_Op), .zero(zero), .op_2(npc_op_1_op_2));
endmodule

// EXT_Op
module EXT (
  input  [1:0] EXT_Op,
  input  [15:0] Input_16,
  output [31:0] Output_32
);

  wire [31:0] bit_extender_1_out, bit_extender_2_out;

  assign bit_extender_1_out = {{16{Input_16[15]}}, Input_16};  // Bit_Extender bit_extender_1
  assign bit_extender_2_out = {{16{1'b0}}, Input_16};  // Bit_Extender bit_extender_2
  Multiplexer #(.select(2), .width(32), .enable("false")) multiplexer_1 (
    .in0(bit_extender_1_out), .in1(bit_extender_2_out), .in2({Input_16, {16{1'b0}}}), .out(Output_32),
    .sel(EXT_Op));  // open: in3
endmodule

// Op
module NPC_Op (
  input  [1:0] Op,
  input  zero,
  output [1:0] op_2
);

  wire and_1_out, and_2_out;

  and and_1 (and_1_out, Op[0], zero);
  and and_2 (and_2_out, Op[1], Op[0]);
  or or_1 (op_2[0], and_1_out, and_2_out);

  assign op_2[1] = Op[1];
endmodule
