// Logisim project LRU.circ as structural Verilog: 5 circuits, main circuit LRU
module LRU (
  input  [15:0] Cnt_0,
  input  [15:0] Cnt_1,
  input  [15:0] Cnt_2,
  input  [15:0] Cnt_3,
  input  Hit_0,
  input  Hit_1,
  input  Hit_2,
  input  Hit_3,
  input  MemRead,
  input  MemWrite,
  input  EN,
  output WE_0,
  output WE_1,
  output WE_2,
  output WE_3
);

  wire [1:0] maxsel_1_max;

  MaxSel maxsel_1 (.Cnt_0(Cnt_0), .Cnt_1(Cnt_1), .Cnt_2(Cnt_2), .Cnt_3(Cnt_3), .Max(maxsel_1_max));
  Renew renew_1 (
    .Hit_0(Hit_0), .Hit_1(Hit_1), .Max(maxsel_1_max), .Hit_2(Hit_2), .Hit_3(Hit_3), .MemRead(MemRead),
    .MemWrite(MemWrite), .EN(EN), .out_9(WE_0), .out_10(WE_1), .out_11(WE_2), .out_12(WE_3));
endmodule

module MaxSel (
  input  [15:0] Cnt_0,
  input  [15:0] Cnt_1,
  input  [15:0] Cnt_2,
  input  [15:0] Cnt_3,
  output [1:0] Max
);

  wire cmp_1_out_3, cmp_2_out_3;
  wire [15:0] cmp_1_out_4, cmp_2_out_4;

  Cmp cmp_1 (.A(Cnt_0), .B(Cnt_1), .out_3(cmp_1_out_3), .out_4(cmp_1_out_4));
  Cmp cmp_2 (.A(Cnt_2), .B(Cnt_3), .out_3(cmp_2_out_3), .out_4(cmp_2_out_4));
  Cmp cmp_3 (.A(cmp_1_out_4), .B(cmp_2_out_4), .out_3(Max[1]));  // open: out_4
  Multiplexer #(.enable("false")) multiplexer_1 (.in0(cmp_1_out_3), .in1(cmp_2_out_3), .out(Max[0]), .sel(Max[1]));
endmodule

module Cmp (
  input  [15:0] A,
  input  [15:0] B,
  output out_3,
  output [15:0] out_4
);

  wire comparator_1_eq, comparator_1_gt, or_1_out;

  Comparator #(.width(16), .mode("unsigned")) comparator_1 (
    .a(A), .b(B), .gt(comparator_1_gt), .eq(comparator_1_eq));  // open: lt
  or or_1 (or_1_out, comparator_1_gt, comparator_1_eq);
  not not_1 (out_3, or_1_out);
  Multiplexer #(.width(16), .enable("false")) multiplexer_1 (.in0(A), .in1(B), .out(out_4), .sel(out_3));
endmodule

module Renew (
  input  Hit_0,
  input  Hit_1,
  input  [1:0] Max,
  input  Hit_2,
  input  Hit_3,
  input  MemRead,
  input  MemWrite,
  input  EN,
  output out_9,
  output out_10,
  output out_11,
  output out_12
);

  wire and_1_out, and_2_out, and_3_out, and_4_out, decoder_1_out0, decoder_1_out1, decoder_1_out2,
       decoder_1_out3, not_1_out, or_1_out, or_2_out, or_3_out;
  wire [1:0] multiplexer_1_out, n4_2_encoder_1_out_5;

  or or_1 (or_1_out, MemRead, MemWrite);
  and and_1 (and_1_out, or_1_out, EN);
  or or_2 (or_2_out, Hit_0, Hit_1, Hit_2, Hit_3);
  and and_2 (and_2_out, or_2_out, MemWrite);
  and and_3 (and_3_out, ~or_2_out, ~MemWrite);  // AND_Gate
  _4_2_Encoder u_4_2_encoder_1 (.a(Hit_3), .b(Hit_2), .c(Hit_1), .d(Hit_0), .out_5(n4_2_encoder_1_out_5));
  Multiplexer #(.width(2), .enable("false")) multiplexer_1 (
    .in0(n4_2_encoder_1_out_5), .in1(Max), .out(multiplexer_1_out), .sel(not_1_out));
  not not_1 (not_1_out, and_2_out);
  or or_3 (or_3_out, and_2_out, and_3_out);
  Decoder #(.select(2), .enable("false")) decoder_1 (
    .out0(decoder_1_out0), .out1(decoder_1_out1), .out2(decoder_1_out2), .out3(decoder_1_out3),
    .sel(multiplexer_1_out));
  and and_4 (and_4_out, or_3_out, and_1_out);
  and and_5 (out_9, decoder_1_out0, and_4_out);
  and and_6 (out_10, decoder_1_out1, and_4_out);
  and and_7 (out_11, decoder_1_out2, and_4_out);
  and and_8 (out_12, decoder_1_out3, and_4_out);
endmodule

module _4_2_Encoder (
  input  a,
  input  b,
  input  c,
  input  d,
  output [1:0] out_5
);

  or or_1 (out_5[1], b, a);
  or or_2 (out_5[0], c, a);
endmodule
